// Logisim project Clocked SR NOR Latch w Probes.circ as structural Verilog: 1 circuit, main circuit main
module main (
  input  R,
  input  S,
  output Q,
  output nQ
);

  wire and_1_out, and_2_out, clock_1_out;

  Clock clock_1 (.out(clock_1_out));
  and and_1 (and_1_out, R, clock_1_out);
  and and_2 (and_2_out, clock_1_out, S);
  // Probe on and_1_out
  // Probe on and_2_out
  nor nor_1 (Q, and_1_out, nQ);
  nor nor_2 (nQ, Q, and_2_out);
endmodule
