// Logisim project 2.circ as structural Verilog: 1 circuit, main circuit main
module main (
);

  wire A, and_1_out, and_2_out, and_3_out, and_4_out, B, C, clock_1_out, D, f, go, not_1_out, not_2_out,
       Reset_out, t_ff_1_q, t_ff_2_q, t_ff_3_q, t_ff_4_q;

  // Probe on {A, B, C, D}
  T_Flip_Flop t_ff_1 (.clk(clock_1_out), .T(1'b1), .Q(t_ff_1_q), .Qn(D), .preset(Reset_out), .en(go));  // open: reset
  Clock clock_1 (.out(clock_1_out));
  // Probe on f
  T_Flip_Flop t_ff_2 (.clk(t_ff_1_q), .T(1'b1), .Q(t_ff_2_q), .Qn(C), .preset(Reset_out));  // open: reset, en
  not not_1 (not_1_out, C);
  TTY #(.rows(1), .cols(18)) tty_1 (.data({6'b011000, f}), .clk(clock_1_out), .we(go), .clr(Reset_out));
  T_Flip_Flop t_ff_3 (.clk(t_ff_2_q), .T(1'b1), .Q(t_ff_3_q), .Qn(B), .preset(Reset_out));  // open: reset, en
  not not_2 (not_2_out, D);
  T_Flip_Flop t_ff_4 (.clk(t_ff_3_q), .T(1'b1), .Q(t_ff_4_q), .Qn(A), .preset(Reset_out));  // open: reset, en
  Button Reset (.out(Reset_out));
  T_Flip_Flop t_ff_5 (.clk(t_ff_4_q), .T(1'b1), .Q(go), .preset(Reset_out));  // open: Qn, reset, en
  and and_1 (and_1_out, C, not_1_out, not_2_out);
  and and_2 (and_2_out, A, not_1_out, not_2_out);
  and and_3 (and_3_out, C, C, D);
  and and_4 (and_4_out, A, C, D);
  or or_1 (f, and_1_out, and_2_out, and_3_out, and_4_out);

  // Notes on the sheet:
  //   000010011001d00d
endmodule
