// Logisim project 3.circ as structural Verilog: 1 circuit, main circuit main
module main (
);

  wire A, B, C, clock_1_out, D, E, F, go, Reset_out, t_ff_1_q, t_ff_2_q, t_ff_3_q, t_ff_4_q, t_ff_5_q,
       t_ff_7_q, X0, X1, X2;
  wire [2:0] multiplexer_1_out, multiplexer_2_out;

  Multiplexer #(.select(3), .width(3)) multiplexer_1 (
    .in0(3'b000), .in1(3'b001), .in2(3'b001), .in3(3'b010), .in4(3'b001), .in5(3'b010), .in6(3'b010),
    .in7(3'b011), .out(multiplexer_1_out), .sel({C, B, A}));  // open: en
  Multiplexer #(.select(3), .width(3)) multiplexer_2 (
    .in0(3'b000), .in1(3'b001), .in2(3'b001), .in3(3'b010), .in4(3'b001), .in5(3'b010), .in6(3'b010),
    .in7(3'b011), .out(multiplexer_2_out), .sel({F, E, D}));  // open: en
  Adder #(.width(3)) adder_1 (.a(multiplexer_1_out), .b(multiplexer_2_out), .out({X2, X1, X0}));  // open: cin, cout
  // Probe on {A, B, C, D, E, F}
  // Probe on {X2, X1, X0}
  Clock clock_1 (.out(clock_1_out));
  TTY #(.rows(1), .cols(65)) tty_1 (.data({4'b0110, X2, X1, X0}), .clk(clock_1_out), .we(go), .clr(Reset_out));
  T_Flip_Flop t_ff_1 (.clk(clock_1_out), .T(1'b1), .Q(t_ff_1_q), .Qn(F), .preset(Reset_out), .en(go));  // open: reset
  T_Flip_Flop t_ff_2 (.clk(t_ff_1_q), .T(1'b1), .Q(t_ff_2_q), .Qn(E), .preset(Reset_out));  // open: reset, en
  T_Flip_Flop t_ff_3 (.clk(t_ff_2_q), .T(1'b1), .Q(t_ff_3_q), .Qn(D), .preset(Reset_out));  // open: reset, en
  T_Flip_Flop t_ff_4 (.clk(t_ff_3_q), .T(1'b1), .Q(t_ff_4_q), .Qn(C), .preset(Reset_out));  // open: reset, en
  T_Flip_Flop t_ff_5 (.clk(t_ff_4_q), .T(1'b1), .Q(t_ff_5_q), .Qn(B), .preset(Reset_out));  // open: reset, en
  T_Flip_Flop t_ff_6 (.clk(t_ff_7_q), .T(1'b1), .Q(go), .preset(Reset_out));  // open: Qn, reset, en
  T_Flip_Flop t_ff_7 (.clk(t_ff_5_q), .T(1'b1), .Q(t_ff_7_q), .Qn(A), .preset(Reset_out));  // open: reset, en
  Button Reset (.out(Reset_out));

  // Notes on the sheet:
  //   0112122312232334122323342334344512232334233434452334344534454556
endmodule
