// Logisim project 6.circ as structural Verilog: 1 circuit, main circuit main
module main (
);

  wire and_1_out, and_2_out, and_3_out, and_4_out, and_5_out, and_6_out, and_7_out, and_8_out, and_9_out,
       clock_1_out, multiplexer_1_out, not_1_out, not_2_out, not_3_out, not_4_out, s0, s1, s2, stop, w0, w1,
       w2, w3, w4, w5, w6, w7, y;

  not not_1 (not_1_out, s0);
  not not_2 (not_2_out, s1);
  not not_3 (not_3_out, s2);
  and and_1 (and_1_out, not_1_out, w0, not_2_out, not_3_out);
  and and_2 (and_2_out, s0, w1, not_2_out, not_3_out);
  and and_3 (and_3_out, not_1_out, w2, s1, not_3_out);
  and and_4 (and_4_out, s0, w3, s1, not_3_out);
  and and_5 (and_5_out, not_1_out, w4, not_2_out, s2);
  and and_6 (and_6_out, s0, w5, not_2_out, s2);
  and and_7 (and_7_out, not_1_out, w6, s1, s2);
  and and_8 (and_8_out, s0, w7, s1, s2);
  or or_1 (y, and_8_out, and_7_out, and_6_out, and_5_out, and_4_out, and_3_out, and_2_out, and_1_out);
  // Probe on {w7, w6, w5, w4, w3, w2, w1, w0}
  Counter #(.width(11), .max('h7ff), .ongoal("stay")) counter_1 (
    .Q({w7, w6, w5, w4, w3, w2, w1, w0, s2, s1, s0}), .clk(and_9_out));  // open: load, D, count, carry, clr
  and and_9 (and_9_out, not_4_out, clock_1_out);
  not not_4 (not_4_out, stop);
  Clock clock_1 (.out(clock_1_out));
  // Probe on {s2, s1, s0}
  Multiplexer #(.select(3)) multiplexer_1 (
    .in0(w0), .in1(w1), .in2(w2), .in3(w3), .in4(w4), .in5(w5), .in6(w6), .in7(w7), .out(multiplexer_1_out),
    .sel({s2, s1, s0}));  // open: en
  xor xor_1 (stop, y, multiplexer_1_out);

  // Notes on the sheet:
  //   In Simulate menu, set tick frequency to 2KHz.
  //   If not then there is an error at the given w7-w0, s0-s2 combination.
  //   Ctrl-R, then Ctrl-K.  w7-w0 should end up being 11111111, ans s2-s0 111.
endmodule
