// Logisim project 2test.circ as structural Verilog: 1 circuit, main circuit main
module main (
  input  in_1,
  input  in_2,
  output nQ
);

  wire _4_Counter_carry, and_1_out, and_2_out, CLK, clock_1_out, go, J, K, or_1_out, or_2_out, Q, Reset_out;
  wire [3:0] _4_Counter_q;

  and and_1 (and_1_out, in_1, K, CLK);
  and and_2 (and_2_out, CLK, J, in_2);
  or or_1 (or_1_out, and_1_out, in_2);
  or or_2 (or_2_out, in_1, and_2_out);
  not not_1 (in_1, or_1_out);
  not not_2 (in_2, or_2_out);
  TTY #(.rows(1), .cols(16)) tty_1 (.data({6'b011000, Q}), .clk(CLK), .we(go), .clr(Reset_out));
  Button Reset (.out(Reset_out));
  Clock clock_1 (.out(clock_1_out));
  // Probe on _4_Counter_q
  Counter #(.width(4), .max('hf)) _4_Counter (
    .Q(_4_Counter_q), .carry(_4_Counter_carry), .clk(CLK), .clr(Reset_out));  // open: load, D, count
  and and_3 (CLK, clock_1_out, go);
  not not_3 (go, _4_Counter_carry);
  // Probe on J
  ROM #(.addrWidth(4), .dataWidth(2)) rom_1 (.addr(_4_Counter_q), .data({K, J}));  // open: sel
  // Probe on K

  // Notes on the sheet:
  //   001100111101000
  //   contents of rom_1 (hex, n*v repeats v):
  //   0 1 0 2 0 3 0 1 1 2 1 3 2 2 3 3
endmodule
