// Logisim project 4.circ as structural Verilog: 1 circuit, main circuit main
module main (
);

  wire _4_Counter_carry, A, AB_nC_out, B, C, CLK, clock_1_out, go, nA, nA_nBw_out, nA_nC_nw_out,
       nAB_nC_nw_out, nAB_out, nABC_out, nABw_out, nAC_2_out, nAC_out, nB, nC, not_1_out, or_1_out, or_2_out,
       or_3_out, Q, Reset_out, w;
  wire [1:0] _4_Counter_q;
  wire [4:0] _32_Counter_q;

  not not_1 (not_1_out, w);
  and AB_nC (AB_nC_out, A, B, nC);
  and nABw (nABw_out, nA, B, w);
  and nABC (nABC_out, nA, B, C);
  and nAB (nAB_out, nA, B);
  and nAC (nAC_out, nA, C);
  and nA_nC_nw (nA_nC_nw_out, nA, nC, not_1_out);
  and nAC_2 (nAC_2_out, nA, C);
  and nA_nBw (nA_nBw_out, nA, nB, w);
  and nAB_nC_nw (nAB_nC_nw_out, nA, B, nC, not_1_out);
  and and_1 (Q, nB, A, w);
  or or_1 (or_1_out, AB_nC_out, nABw_out, nABC_out);
  or or_2 (or_2_out, nAB_out, nAC_out, nA_nC_nw_out);
  or or_3 (or_3_out, nAC_2_out, nA_nBw_out, nAB_nC_nw_out);
  D_Flip_Flop d_ff_1 (.clk(CLK), .D(or_1_out), .Q(A), .Qn(nA));  // open: preset, en, reset
  D_Flip_Flop d_ff_2 (.clk(CLK), .D(or_2_out), .Q(B), .Qn(nB));  // open: preset, en, reset
  D_Flip_Flop d_ff_3 (.clk(CLK), .D(or_3_out), .Q(C), .Qn(nC));  // open: preset, en, reset
  TTY #(.rows(17), .cols(4)) tty_1 (.data({6'b011000, Q}), .clk(CLK), .we(go), .clr(Reset_out));
  Button Reset (.out(Reset_out));
  and and_2 (CLK, clock_1_out, go);
  Clock clock_1 (.out(clock_1_out));
  // Probe on _4_Counter_q
  Counter #(.width(2), .max('h3)) _4_Counter (
    .Q(_4_Counter_q), .carry(_4_Counter_carry), .clk(CLK), .clr(Reset_out));  // open: load, D, count
  // Probe on _32_Counter_q[3:0]
  Counter #(.width(5), .max('h1f), .trigger("falling")) _32_Counter (
    .Q(_32_Counter_q), .clk(_4_Counter_carry), .clr(Reset_out));  // open: load, D, count, carry
  // Probe on w
  BitSelector #(.width(4)) bitselector_1 (.in(_32_Counter_q[3:0]), .out(w), .sel(_4_Counter_q));
  not not_2 (go, _32_Counter_q[4]);

  // Notes on the sheet:
  //   0000
  //   1000
  //   0100
  //   1100
  //   0010
  //   1010
  //   0110
  //   1110
  //   0001
  //   1001
  //   0101
  //   1101
  //   0011
  //   1011
  //   0111
  //   1111
  //   1
  //   1
  //   11 gates
endmodule
