// Logisim project 5.circ as structural Verilog: 1 circuit, main circuit main
module main (
);

  wire _5_Counter_carry, and_1_out, and_2_out, and_3_out, and_4_out, and_5_out, and_6_out, and_7_out,
       and_8_out, CLK, clock_1_out, d_ff_1_q, d_ff_1_qn, d_ff_2_q, d_ff_2_qn, d_ff_3_q, d_ff_3_qn, go,
       not_1_out, not_2_out, or_1_out, or_2_out, or_3_out, or_4_out, p, Reset_out, t_ff_1_q, t_ff_1_qn, w;
  wire [2:0] _5_Counter_q;
  wire [5:0] _64_Counter_q;

  not not_1 (not_1_out, w);
  // Probe on w
  not not_2 (not_2_out, and_8_out);
  and and_1 (and_1_out, d_ff_1_q, d_ff_3_qn);
  and and_2 (and_2_out, d_ff_2_q, d_ff_3_q);
  and and_3 (and_3_out, d_ff_2_q, d_ff_3_qn);
  and and_4 (and_4_out, d_ff_1_qn, d_ff_2_qn, d_ff_3_q);
  and and_5 (and_5_out, and_8_out, t_ff_1_q, not_1_out);
  and and_6 (and_6_out, not_2_out, w);
  and and_7 (and_7_out, t_ff_1_qn, w);
  or or_1 (or_1_out, and_1_out, and_2_out);
  or or_2 (or_2_out, and_3_out, and_4_out);
  or or_3 (or_3_out, d_ff_3_qn, d_ff_1_q);
  or or_4 (or_4_out, and_5_out, and_6_out, and_7_out);
  // Probe on t_ff_1_q
  D_Flip_Flop d_ff_1 (.clk(CLK), .D(or_1_out), .Q(d_ff_1_q), .Qn(d_ff_1_qn));  // open: preset, en, reset
  D_Flip_Flop d_ff_2 (.clk(CLK), .D(or_2_out), .Q(d_ff_2_q), .Qn(d_ff_2_qn));  // open: preset, en, reset
  D_Flip_Flop d_ff_3 (.clk(CLK), .D(or_3_out), .Q(d_ff_3_q), .Qn(d_ff_3_qn));  // open: preset, en, reset
  // Probe on t_ff_1_qn
  T_Flip_Flop t_ff_1 (.clk(CLK), .T(or_4_out), .Q(t_ff_1_q), .Qn(t_ff_1_qn));  // open: preset, reset, en
  // Probe on d_ff_1_q
  // Probe on d_ff_2_q
  // Probe on d_ff_3_q
  and and_8 (and_8_out, d_ff_1_q, d_ff_3_q);
  // Probe on and_8_out
  and and_9 (p, and_8_out, t_ff_1_qn);
  TTY #(.rows(33), .cols(5)) tty_1 (.data({6'b011000, p}), .clk(CLK), .we(go), .clr(Reset_out));
  Button Reset (.out(Reset_out));
  // Probe on w
  nand nand_1 (go, _64_Counter_q[0], _64_Counter_q[5]);
  Counter #(.width(3), .max('h4)) _5_Counter (
    .Q(_5_Counter_q), .carry(_5_Counter_carry), .clk(CLK), .clr(Reset_out));  // open: load, D, count
  and and_10 (CLK, clock_1_out, go);
  Clock clock_1 (.out(clock_1_out));
  Counter #(.width(6), .max('h3f), .trigger("falling")) _64_Counter (
    .Q(_64_Counter_q), .clk(_5_Counter_carry), .clr(Reset_out));  // open: load, D, count, carry
  // Probe on _5_Counter_q
  // Probe on _64_Counter_q
  BitSelector #(.width(6)) bitselector_1 (.in(_64_Counter_q), .out(w), .sel(_5_Counter_q));

  // Notes on the sheet:
  //   1  0
  //   1  3
  //   1  5
  //   1  6
  //   1  9
  //   1   10
  //   1  12
  //   1  15
  //   1  17
  //   1  18
  //   1  20
  //   1  23
  //   1  24
  //   1 27
  //   1  29
  //   1  30
  //   24 Gates
endmodule
