// Logisim project 6.circ as structural Verilog: 1 circuit, main circuit main
module main (
);

  wire _4_Counter_carry, A, and_1_out, and_2_out, and_3_out, and_4_out, and_5_out, and_6_out, and_7_out,
       and_8_out, and_9_out, and_10_out, and_11_out, and_12_out, and_14_out, and_15_out, B, C, CLK,
       clock_1_out, go, I5, I10, I25, nA, nB, nC, O5, O10, OM, or_1_out, or_2_out, or_3_out, Reset_out;
  wire [4:0] _4_Counter_q;

  and and_1 (and_1_out, nA, B, C, I5);
  and and_2 (and_2_out, nB, C, I10);
  and and_3 (and_3_out, nB, I5);
  and and_4 (and_4_out, nA, C, I5);
  and and_5 (and_5_out, nB, C, I10);
  and and_6 (and_6_out, B, nC, I10);
  and and_7 (and_7_out, nA, B, I5);
  and and_8 (and_8_out, nA, C, I5);
  and and_9 (and_9_out, nC, I10);
  and and_10 (and_10_out, nB, I10);
  and and_11 (and_11_out, A, I10);
  and and_12 (and_12_out, B, I25);
  and and_13 (O10, C, I25);
  and and_14 (and_14_out, A, I5);
  and and_15 (and_15_out, B, C, I10);
  or or_1 (or_1_out, and_1_out, and_2_out);
  or or_2 (or_2_out, and_3_out, and_4_out, and_5_out, and_6_out);
  or or_3 (or_3_out, and_7_out, and_8_out, and_9_out, and_10_out);
  or or_4 (O5, and_11_out, and_12_out);
  or or_5 (OM, and_14_out, I25, and_15_out);
  D_Flip_Flop d_ff_1 (.clk(CLK), .D(or_1_out), .Q(A), .Qn(nA));  // open: preset, en, reset
  D_Flip_Flop d_ff_2 (.clk(CLK), .D(or_2_out), .Q(B), .Qn(nB));  // open: preset, en, reset
  D_Flip_Flop d_ff_3 (.clk(CLK), .D(or_3_out), .Q(C), .Qn(nC));  // open: preset, en, reset
  TTY #(.rows(1), .cols(33)) tty_1 (.data({4'b1000, OM, O10, O5}), .clk(CLK), .we(go), .clr(Reset_out));
  Button Reset (.out(Reset_out));
  // Probe on _4_Counter_q
  Counter #(.width(5), .max('h1f)) _4_Counter (
    .Q(_4_Counter_q), .carry(_4_Counter_carry), .clk(CLK), .clr(Reset_out));  // open: load, D, count
  and and_16 (CLK, clock_1_out, go);
  Clock clock_1 (.out(clock_1_out));
  not not_1 (go, _4_Counter_carry);
  ROM #(.addrWidth(5), .dataWidth(3)) rom_1 (.addr(_4_Counter_q), .data({I25, I10, I5}));  // open: sel
  // Probe on I5
  // Probe on I25
  // Probe on I10

  // Notes on the sheet:
  //   24 Gates
  //   D@@@@D@@@D@@E@E@F@@G@@G@F@@E@@@
  //   contents of rom_1 (hex, n*v repeats v):
  //   4 6*1 2 1 1 2 2 2 1 4 2 4 2 2 4 1 2 4 2 4 2 2 2 1 1 1 2
endmodule
