// Logisim project 7.circ as structural Verilog: 1 circuit, main circuit main
module main (
);

  wire A0, A1, A2, A3, Ad0, Ad1, Ad2, Ad3, and_2_out, and_3_out, and_4_out, and_5_out, and_6_out, and_7_out,
       and_8_out, and_9_out, and_10_out, and_11_out, and_12_out, and_13_out, B0, B1, B2, B3, C0, C1, C2, C3,
       C4, CIN, clock_1_out, go, or_2_out, or_3_out, or_4_out, or_5_out, or_6_out, or_7_out, or_8_out,
       Reset_out, S0, S1, t_ff_1_q, t_ff_2_q, t_ff_3_q, t_ff_4_q, xor_1_out, xor_3_out, xor_5_out, xor_7_out;
  wire [3:0] and_1_out, not_1_out, or_1_out, xor_2_out;
  wire [11:11] rom_1_data;

  assign and_1_out = {A3, A2, A1, A0} & {B3, B2, B1, B0};  // AND_Gate and_1, 4 bits wide
  assign or_1_out = {A3, A2, A1, A0} | {B3, B2, B1, B0};  // OR_Gate or_1, 4 bits wide
  or or_2 (or_2_out, A0, B0);
  and and_2 (and_2_out, CIN, or_2_out);
  and and_3 (and_3_out, A0, B0);
  assign not_1_out = ~{A3, A2, A1, A0};  // NOT_Gate not_1, 4 bits wide
  Multiplexer #(.select(2), .width(4)) multiplexer_1 (
    .in0(and_1_out), .in1(or_1_out), .in2(not_1_out), .in3(xor_2_out), .out({C3, C2, C1, C0}), .sel({S1, S0}));  // open: en
  xor xor_1 (xor_1_out, A0, B0);
  or or_3 (or_3_out, and_3_out, and_2_out);
  xor xor_2 (xor_2_out[0], CIN, xor_1_out);
  or or_4 (or_4_out, A1, B1);
  and and_4 (and_4_out, or_3_out, or_4_out);
  xor xor_3 (xor_3_out, A1, B1);
  and and_5 (and_5_out, A1, B1);
  or or_5 (or_5_out, and_5_out, and_4_out);
  xor xor_4 (xor_2_out[1], or_3_out, xor_3_out);
  or or_6 (or_6_out, A2, B2);
  and and_6 (and_6_out, or_5_out, or_6_out);
  xor xor_5 (xor_5_out, A2, B2);
  and and_7 (and_7_out, A2, B2);
  or or_7 (or_7_out, and_7_out, and_6_out);
  xor xor_6 (xor_2_out[2], or_5_out, xor_5_out);
  or or_8 (or_8_out, A3, B3);
  and and_8 (and_8_out, or_7_out, or_8_out);
  xor xor_7 (xor_7_out, A3, B3);
  and and_9 (and_9_out, A3, B3);
  // OR_Gate or_9 has open pins: in0=and_9_out, in1=and_8_out, out=open
  xor xor_8 (xor_2_out[3], or_7_out, xor_7_out);
  and and_10 (and_10_out, or_8_out, and_7_out);
  and and_11 (and_11_out, or_8_out, or_6_out, and_5_out);
  and and_12 (and_12_out, or_8_out, or_6_out, or_4_out, and_3_out);
  and and_13 (and_13_out, or_8_out, or_6_out, or_4_out, or_2_out, CIN);
  or or_10 (C4, and_9_out, and_10_out, and_11_out, and_12_out, and_13_out);
  Clock clock_1 (.out(clock_1_out));
  T_Flip_Flop t_ff_1 (.clk(clock_1_out), .T(1'b1), .Q(t_ff_1_q), .Qn(Ad0), .preset(Reset_out), .en(go));  // open: reset
  // Probe on {C4, C3, C2, C1, C0}
  T_Flip_Flop t_ff_2 (.clk(t_ff_1_q), .T(1'b1), .Q(t_ff_2_q), .Qn(Ad1), .preset(Reset_out));  // open: reset, en
  // Probe on {S1, S0}
  // Probe on CIN
  TTY #(.rows(1), .cols(16)) tty_1 (.data({2'b10, C4, C3, C2, C1, C0}), .clk(clock_1_out), .we(go), .clr(Reset_out));
  T_Flip_Flop t_ff_3 (.clk(t_ff_2_q), .T(1'b1), .Q(t_ff_3_q), .Qn(Ad2), .preset(Reset_out));  // open: reset, en
  // Probe on {rom_1_data[11], CIN, S1, S0, B3, B2, B1, B0, A3, A2, A1, A0}
  ROM #(.addrWidth(4), .dataWidth(12)) rom_1 (
    .addr({Ad3, Ad2, Ad1, Ad0}), .data({rom_1_data[11], CIN, S1, S0, B3, B2, B1, B0, A3, A2, A1, A0}));  // open: sel
  // Probe on {B3, B2, B1, B0}
  T_Flip_Flop t_ff_4 (.clk(t_ff_3_q), .T(1'b1), .Q(t_ff_4_q), .Qn(Ad3), .preset(Reset_out));  // open: reset, en
  T_Flip_Flop t_ff_5 (.clk(t_ff_4_q), .T(1'b1), .Q(go), .preset(Reset_out));  // open: Qn, reset, en
  // Probe on {A3, A2, A1, A0}
  Button Reset (.out(Reset_out));

  // Notes on the sheet:
  //   adds 64 to make printable
  //   contents of rom_1 (hex, n*v repeats v):
  //   0 4ff ac 100 5ff 1ac 200 6ff 2ac 300 7ff 3ac 3c3 73c 37d 7d7
  //   @_X@_^OPS@_VOPTU
endmodule
