// Logisim project Lab1.circ as structural Verilog: 8 circuits, main circuit main
module main (
);

  wire Clock, ROMSeqOut, sequentialinput_1_notdone, X;
  wire [2:0] CombOut, ROMCombOut;
  wire [7:0] Input;

  Clock clock_1 (.out(Clock));
  CombinationalInput combinationalinput_1 (
    .In7(Input[7]), .In6(Input[6]), .In5(Input[5]), .In4(Input[4]), .In3(Input[3]), .In2(Input[2]),
    .In1(Input[1]), .In0(Input[0]), .Clock(Clock));
  SequentialInput sequentialinput_1 (.X(X), .NotDone(sequentialinput_1_notdone), .Clock(Clock));
  Comb Comb (.In(Input), .Out(CombOut));
  ROMComb ROMComb (.Input(Input), .Output(ROMCombOut));
  ROMSeq ROMSeq (.X(X), .Select(sequentialinput_1_notdone), .Clock(Clock), .Out(ROMSeqOut));
  // Probe on Input
  // Probe on CombOut
  // Probe on ROMCombOut
  // Probe on X
  // Probe on ROMSeqOut
endmodule

module CombinationalInput (
  input  Clock,
  output In7,
  output In6,
  output In5,
  output In4,
  output In3,
  output In2,
  output In1,
  output In0
);

  wire [7:0] counter_1_q;

  Counter #(.ongoal("stay")) counter_1 (.count(1'b1), .Q(counter_1_q), .clk(Clock));  // open: load, D, carry, clr
  ROM rom_1 (.addr(counter_1_q), .data({In7, In6, In5, In4, In3, In2, In1, In0}));  // open: sel

  // Notes on the sheet:
  //   contents of rom_1 (hex, n*v repeats v):
  //   0 1 2 3 4 5 6 7 8 9 a b c d e f 10 11 12 13 14 15 16 17 18 19 1a 1b 1c 1d 1e 1f 20 21 22 23 24 25 26
  //   27 28 29 2a 2b 2c 2d 2e 2f 30 31 32 33 34 35 36 37 38 39 3a 3b 3c 3d 3e 3f 40 41 42 43 44 45 46 47
  //   48 49 4a 4b 4c 4d 4e 4f 50 51 52 53 54 55 56 57 58 59 5a 5b 5c 5d 5e 5f 60 61 62 63 64 65 66 67 68
  //   69 6a 6b 6c 6d 6e 6f 70 71 72 73 74 75 76 77 78 79 7a 7b 7c 7d 7e 7f 80 81 82 83 84 85 86 87 88 89
  //   8a 8b 8c 8d 8e 8f 90 91 92 93 94 95 96 97 98 99 9a 9b 9c 9d 9e 9f a0 a1 a2 a3 a4 a5 a6 a7 a8 a9 aa
  //   ab ac ad ae af b0 b1 b2 b3 b4 b5 b6 b7 b8 b9 ba bb bc bd be bf c0 c1 c2 c3 c4 c5 c6 c7 c8 c9 ca cb
  //   cc cd ce cf d0 d1 d2 d3 d4 d5 d6 d7 d8 d9 da db dc dd de df e0 e1 e2 e3 e4 e5 e6 e7 e8 e9 ea eb ec
  //   ed ee ef f0 f1 f2 f3 f4 f5 f6 f7 f8 f9 fa fb fc fd fe ff
endmodule

module SequentialInput (
  input  Clock,
  output X,
  output NotDone
);

  wire comparator_1_eq, counter_2_q;
  wire [7:0] counter_1_q;

  Counter #(.max('h9f), .ongoal("stay")) counter_1 (
    .count(1'b1), .Q(counter_1_q), .clk(Clock));  // open: load, D, carry, clr
  Comparator comparator_1 (.a(counter_1_q), .b(8'h9f), .eq(comparator_1_eq));  // open: gt, lt
  ROM #(.dataWidth(1)) rom_1 (.addr(counter_1_q), .data(X));  // open: sel
  Counter #(.width(1), .max('h1), .ongoal("stay")) counter_2 (
    .count(comparator_1_eq), .Q(counter_2_q), .clk(Clock));  // open: load, D, carry, clr
  not not_1 (NotDone, counter_2_q);

  // Notes on the sheet:
  //   contents of rom_1 (hex, n*v repeats v):
  //   9*0 1 0 0 0 1 4*0 1 1 0 0 1 4*0 1 0 1 0 0 1 1 0 0 0 1 1 1 0 1 4*0 1 0 0 1 0 1 0 1 0 0 1 0 1 1 0 1 1
  //   0 0 0 1 1 0 1 0 1 1 1 0 0 5*1 4*0 1 0 0 0 1 1 0 0 1 0 1 0 0 1 1 1 0 1 0 0 1 0 1 0 1 1 0 1 1 0 1 0
  //   5*1 0 0 0 1 1 0 0 1 1 1 0 1 0 1 1 0 5*1 0 0 1 1 1 0 5*1 0 5*1
endmodule

module ROMXOR (
  input  X,
  input  Y,
  output X_XOR_Y
);

  ROM #(.addrWidth(2), .dataWidth(1)) rom_1 (.addr({X, Y}), .data(X_XOR_Y));  // open: sel

  // Notes on the sheet:
  //   contents of rom_1 (hex, n*v repeats v):
  //   0 1 1
endmodule

module ROMSeqEx (
  input  X,
  input  Clock,
  output [1:0] Out
);

  wire [1:1] register_1_q;
  wire [2:0] rom_1_data;

  ROM #(.addrWidth(2), .dataWidth(3)) rom_1 (.addr({register_1_q[1], X}), .data(rom_1_data));  // open: sel
  Register #(.width(3)) register_1 (.D(rom_1_data), .Q({register_1_q[1], Out}), .clk(Clock));  // open: en, clr

  // Notes on the sheet:
  //   contents of rom_1 (hex, n*v repeats v):
  //   1 5 7 3
endmodule

module Comb (
  input  [7:0] In,
  output [2:0] Out
);

  wire and_1_out, and_2_out, and_3_out, and_4_out, and_5_out, and_6_out, and_7_out, and_8_out, not_1_out,
       not_2_out, not_3_out, not_4_out, not_5_out, not_6_out;

  not not_1 (not_1_out, In[0]);
  not not_2 (not_2_out, In[1]);
  not not_3 (not_3_out, In[5]);
  not not_4 (not_4_out, In[4]);
  not not_5 (not_5_out, In[7]);
  not not_6 (not_6_out, In[6]);
  and and_1 (and_1_out, not_5_out, not_3_out, not_2_out, In[0]);
  and and_2 (and_2_out, not_5_out, not_3_out, In[1], not_1_out);
  and and_3 (and_3_out, not_5_out, In[6]);
  and and_4 (and_4_out, In[6], In[4]);
  and and_5 (and_5_out, not_5_out, not_6_out, not_4_out, In[2], not_2_out);
  and and_6 (and_6_out, In[7], In[6]);
  and and_7 (and_7_out, not_5_out, not_6_out, not_4_out, In[1], In[0]);
  and and_8 (and_8_out, not_5_out, not_6_out, not_4_out, In[3]);
  or or_1 (Out[0], and_1_out, and_2_out, and_3_out, and_4_out);
  or or_2 (Out[1], and_5_out, and_6_out);
  or or_3 (Out[2], and_7_out, and_8_out);
endmodule

module ROMComb (
  input  [7:0] Input,
  output [2:0] Output
);

  ROM #(.dataWidth(3)) rom_1 (.addr(Input), .data(Output));  // open: sel

  // Notes on the sheet:
  //   contents of rom_1 (hex, n*v repeats v):
  //   0 0 1 0 2 3 0 4 0 0 5 53*0 16*1 112*0 16*2 16*3
endmodule

module ROMSeq (
  input  X,
  input  Select,
  input  Clock,
  output Out
);

  wire [4:0] rom_1_data;
  wire [4:1] register_1_q;

  ROM #(.addrWidth(5), .dataWidth(5)) rom_1 (.addr({register_1_q, X}), .data(rom_1_data), .sel(Select));
  Register #(.width(5)) register_1 (.D(rom_1_data), .Q({register_1_q, Out}), .clk(Clock));  // open: en, clr

  // Notes on the sheet:
  //   contents of rom_1 (hex, n*v repeats v):
  //   2 4 6 8 8 a c e e 10 10 12 14 14 14 16 16 18 18 18 1a 1a 1a 1c 1c 1c 2 4 3 5
endmodule
