// Logisim project Lab2.circ as structural Verilog: 12 circuits, main circuit main
module main (
);

  wire _0, ALUSrc, Beq, Branch, Clock, Jal, jr, Jump, MemRead, MemtoReg, MemWrite, not_1_out, or_1_out,
       RegDst, WrReg;
  wire [2:0] ALUCtrl, ALUOp;
  wire [4:0] multiplexer_5_out, RegDest;
  wire [5:0] funct;
  wire [7:0] Address;
  wire [15:6] iAddress;
  wire [31:0] adder_2_out, DataRead, DataWrite, InputA, InputB, multiplexer_1_out, multiplexer_2_out,
       multiplexer_4_out, multiplexer_6_out, NextAddr, PC, PC_4, Sign_Extend_2_seout, Sign_Extend_seout,
       sl2_1_out_2, WrData;
  wire [31:8] ALUResult;
  wire [31:16] Instr;

  Clock clock_1 (.out(Clock));
  ALU alu_1 (
    .ALUCtl(ALUCtrl), .A(InputA), .B(InputB), .ALUResult({ALUResult, Address}), .Zero(_0), .Shamt({5{1'b0}}));  // open: Overflow
  and and_1 (Beq, _0, Branch);
  RegFile regfile_1 (
    .WrAddr(RegDest), .WrData(WrData), .WrReg(WrReg), .RdAddr1(Instr[25:21]), .RdAddr2(Instr[20:16]),
    .RdData1(InputA), .RdData2(DataWrite), .Clock(Clock));
  // Probe on {ALUResult, Address}
  PC PC_2 (.PC_Input(NextAddr), .Clock(Clock), .PC_Output(PC));
  Control control_1 (
    .Opcode(Instr[31:26]), .ALUCtr0(ALUOp[0]), .ALUCtrl1(ALUOp[1]), .ALUCtrl2(ALUOp[2]), .RegDst(RegDst),
    .WrReg(WrReg), .ALUSrc(ALUSrc), .MemWrite(MemWrite), .MemtoReg(MemtoReg), .MemRead(MemRead),
    .Branch(Branch), .jump(Jump), .jal(Jal));
  InstrMem instrmem_1 (.InstAddr(PC[9:2]), .Instruction({Instr, iAddress, funct}));
  DataMem datamem_1 (
    .Address(Address), .MemWrite(DataWrite), .Write(MemWrite), .Read(MemRead), .MemRead(DataRead),
    .Clock(Clock));
  Adder #(.width(32)) adder_1 (.a(PC), .b(32'h4), .out(PC_4));  // open: cin, cout
  // Probe on PC_4
  Sign_Extend Sign_Extend (.SEIn({iAddress, funct}), .SEOut(Sign_Extend_seout));
  SL2 sl2_1 (.in_1(Sign_Extend_seout), .out_2(sl2_1_out_2));
  Sign_Extend Sign_Extend_2 (.SEIn({iAddress, funct}), .SEOut(Sign_Extend_2_seout));
  ALU_Control ALU_Ctrl (.OpCode(Instr[31:26]), .ALUOp(ALUOp), .funct(funct), .jr(jr), .ALUCtrl(ALUCtrl));
  Adder #(.width(32)) adder_2 (.a(PC_4), .b(sl2_1_out_2), .out(adder_2_out));  // open: cin, cout
  Multiplexer #(.width(32)) multiplexer_1 (
    .in0(Sign_Extend_2_seout), .in1(DataWrite), .out(multiplexer_1_out), .sel(Branch));  // open: en
  Multiplexer #(.width(32)) multiplexer_2 (
    .in0(PC_4), .in1(adder_2_out), .out(multiplexer_2_out), .sel(Beq));  // open: en
  not not_1 (not_1_out, ALUSrc);
  Multiplexer #(.width(32)) multiplexer_3 (
    .in0(multiplexer_1_out), .in1(DataWrite), .out(InputB), .sel(not_1_out));  // open: en
  Multiplexer #(.width(32)) multiplexer_4 (
    .in0({ALUResult, Address}), .in1(PC_4), .out(multiplexer_4_out), .sel(Jal));  // open: en
  Multiplexer #(.width(5)) multiplexer_5 (
    .in0(Instr[20:16]), .in1(iAddress[15:11]), .out(multiplexer_5_out), .sel(RegDst));  // open: en
  or or_1 (or_1_out, Jump, Jal);
  Multiplexer #(.width(32)) multiplexer_6 (
    .in0(multiplexer_2_out), .in1(sl2_1_out_2), .out(multiplexer_6_out), .sel(or_1_out));  // open: en
  Multiplexer #(.width(5)) multiplexer_7 (
    .in0(multiplexer_5_out), .in1({5{1'b1}}), .out(RegDest), .sel(Jal));  // open: en
  Multiplexer #(.width(32)) multiplexer_8 (
    .in0(multiplexer_6_out), .in1(InputA), .out(NextAddr), .sel(jr));  // open: en
  Multiplexer #(.width(32)) multiplexer_9 (
    .in0(multiplexer_4_out), .in1(DataRead), .out(WrData), .sel(MemRead));  // open: en
  // Probe on PC
  // Probe on Branch
  // Probe on Jump
  // Probe on Jal
  // Probe on jr
  // Probe on WrReg
  // Probe on RegDest
  // Probe on WrData
  // Probe on MemWrite
  // Probe on DataWrite

  // Other names for the same wires on the sheet: ALUResult[7:0] = Address; iAddress[5:0] = funct;
  //   Instr[15:0] = {iAddress, funct}; jAddress[25:0] = {Instr[25:16], iAddress, funct}; shamt[4:0] = iAddress[10:6];
  //   rd[4:0] = iAddress[15:11]; rt[4:0] = Instr[20:16]; rs[4:0] = Instr[25:21]; opcode[5:0] = Instr[31:26];
  //   RData2[31:0] = DataWrite

  // Notes on the sheet:
  //   R-Type
  //   I-Type
  //   J-Type
endmodule

module _32bit (
  input  Add_Sub_control,
  input  [31:0] in_2,
  input  [31:0] in_3,
  output [31:0] out_4,
  output carry_out
);

  wire adder_1_cout, subtractor_1_bout;
  wire [31:0] adder_1_out, subtractor_1_out;

  Adder #(.width(32)) adder_1 (.a(in_2), .b(in_3), .out(adder_1_out), .cout(adder_1_cout));  // open: cin
  Subtractor #(.width(32)) subtractor_1 (
    .a(in_2), .b(in_3), .out(subtractor_1_out), .bout(subtractor_1_bout));  // open: bin
  Multiplexer #(.width(32), .enable("false")) multiplexer_1 (
    .in0(adder_1_out), .in1(subtractor_1_out), .out(out_4), .sel(Add_Sub_control));
  Multiplexer #(.enable("false")) multiplexer_2 (
    .in0(adder_1_cout), .in1(subtractor_1_bout), .out(carry_out), .sel(Add_Sub_control));
endmodule

module ALU (
  input  [2:0] ALUCtl,
  input  [31:0] A,
  input  [31:0] B,
  input  [4:0] Shamt,
  output [31:0] ALUResult,
  output Zero,
  output Overflow
);

  wire and_2_out, and_3_out, comparator_1_lt, not_1_out, not_2_out, not_3_out, or_2_out;
  wire [31:0] Add, And, LessThan, Or, ShiftLeft, ShiftRight, Sub, Xor;

  Adder #(.width(32)) adder_1 (.a(A), .b(B), .out(Add));  // open: cin, cout
  Subtractor #(.width(32)) subtractor_1 (.a(A), .b(B), .out(Sub));  // open: bin, bout
  assign And = A & B;  // AND_Gate and_1, 32 bits wide
  assign Or = A | B;  // OR_Gate or_1, 32 bits wide
  assign Xor = A ^ B;  // XOR_Gate xor_1, 32 bits wide
  Comparator #(.width(32)) comparator_1 (.a(A), .b(B), .lt(comparator_1_lt));  // open: gt, eq
  assign LessThan = {{31{1'b0}}, comparator_1_lt};  // Bit_Extender bit_extender_1
  Shifter #(.width(32)) shifter_1 (.in(B), .\dist (Shamt), .out(ShiftLeft));
  Shifter #(.width(32), .shift("lr")) shifter_2 (.in(B), .\dist (Shamt), .out(ShiftRight));
  Multiplexer #(.select(3), .width(32), .enable("false")) multiplexer_1 (
    .in0(Or), .in1(Xor), .in2(And), .in3(Add), .in4(Sub), .in5(LessThan), .in6(ShiftLeft), .in7(ShiftRight),
    .out(ALUResult), .sel(ALUCtl));
  not not_1 (not_1_out, ALUCtl[0]);
  not not_2 (not_2_out, ALUCtl[1]);
  not not_3 (not_3_out, ALUCtl[2]);
  and and_2 (and_2_out, not_1_out, not_2_out, not_3_out);
  and and_3 (and_3_out, not_1_out, not_2_out, ALUCtl[2]);
  Overflow overflow_1 (
    .Add(and_2_out), .Sub(and_3_out), .ASign(A[31]), .BSign(B[31]), .ResultSign(ALUResult[31]),
    .Overflow(Overflow));
  not not_4 (Zero, or_2_out);
  or or_2 (or_2_out, ALUResult[0], ALUResult[1], ALUResult[2], ALUResult[3], ALUResult[4], ALUResult[5], ALUResult[6], ALUResult[7], ALUResult[8], ALUResult[9], ALUResult[10], ALUResult[11], ALUResult[12], ALUResult[13], ALUResult[14], ALUResult[15], ALUResult[16], ALUResult[17], ALUResult[18], ALUResult[19], ALUResult[20], ALUResult[21], ALUResult[22], ALUResult[23], ALUResult[24], ALUResult[25], ALUResult[26], ALUResult[27], ALUResult[28], ALUResult[29], ALUResult[30], ALUResult[31]);

  // Other names for the same wires on the sheet: ASign = A[31]; ResultSign = ALUResult[31]; BSign = B[31]
endmodule

module RegFile (
  input  [4:0] WrAddr,
  input  [31:0] WrData,
  input  WrReg,
  input  [4:0] RdAddr1,
  input  [4:0] RdAddr2,
  input  Clock,
  output [31:0] RdData1,
  output [31:0] RdData2
);

  wire WrReg0, WrReg1, WrReg2, WrReg3, WrReg4, WrReg5, WrReg6, WrReg7, WrReg8, WrReg9, WrReg10, WrReg11,
       WrReg12, WrReg13, WrReg14, WrReg15, WrReg16, WrReg17, WrReg18, WrReg19, WrReg20, WrReg21, WrReg22,
       WrReg23, WrReg24, WrReg25, WrReg26, WrReg27, WrReg28, WrReg29, WrReg30, WrReg31;
  wire [31:0] RegData1, RegData2, RegData3, RegData4, RegData5, RegData6, RegData7, RegData8, RegData9,
       RegData10, RegData11, RegData12, RegData13, RegData14, RegData15, RegData16, RegData17, RegData18,
       RegData19, RegData20, RegData21, RegData22, RegData23, RegData24, RegData25, RegData26, RegData27,
       RegData28, RegData29, RegData30, RegData31;

  Demultiplexer #(.select(5), .enable("false")) demultiplexer_1 (
    .out0(WrReg0), .out1(WrReg1), .out2(WrReg2), .out3(WrReg3), .out4(WrReg4), .out5(WrReg5), .out6(WrReg6),
    .out7(WrReg7), .out8(WrReg8), .out9(WrReg9), .out10(WrReg10), .out11(WrReg11), .out12(WrReg12),
    .out13(WrReg13), .out14(WrReg14), .out15(WrReg15), .out16(WrReg16), .out17(WrReg17), .out18(WrReg18),
    .out19(WrReg19), .out20(WrReg20), .out21(WrReg21), .out22(WrReg22), .out23(WrReg23), .out24(WrReg24),
    .out25(WrReg25), .out26(WrReg26), .out27(WrReg27), .out28(WrReg28), .out29(WrReg29), .out30(WrReg30),
    .out31(WrReg31), .in(WrReg), .sel(WrAddr));
  Register #(.width(32)) Reg4 (.D(WrData), .en(WrReg4), .Q(RegData4), .clk(Clock));  // open: clr
  Register #(.width(32)) Reg8 (.D(WrData), .en(WrReg8), .Q(RegData8), .clk(Clock));  // open: clr
  Register #(.width(32)) Reg12 (.D(WrData), .en(WrReg12), .Q(RegData12), .clk(Clock));  // open: clr
  Register #(.width(32)) Reg16 (.D(WrData), .en(WrReg16), .Q(RegData16), .clk(Clock));  // open: clr
  Register #(.width(32)) Reg20 (.D(WrData), .en(WrReg20), .Q(RegData20), .clk(Clock));  // open: clr
  Register #(.width(32)) Reg24 (.D(WrData), .en(WrReg24), .Q(RegData24), .clk(Clock));  // open: clr
  Register #(.width(32)) Reg28 (.D(WrData), .en(WrReg28), .Q(RegData28), .clk(Clock));  // open: clr
  Register #(.width(32)) Reg1 (.D(WrData), .en(WrReg1), .Q(RegData1), .clk(Clock));  // open: clr
  Register #(.width(32)) Reg5 (.D(WrData), .en(WrReg5), .Q(RegData5), .clk(Clock));  // open: clr
  Register #(.width(32)) Reg9 (.D(WrData), .en(WrReg9), .Q(RegData9), .clk(Clock));  // open: clr
  Register #(.width(32)) Reg13 (.D(WrData), .en(WrReg13), .Q(RegData13), .clk(Clock));  // open: clr
  Register #(.width(32)) Reg17 (.D(WrData), .en(WrReg17), .Q(RegData17), .clk(Clock));  // open: clr
  Register #(.width(32)) Reg21 (.D(WrData), .en(WrReg21), .Q(RegData21), .clk(Clock));  // open: clr
  Register #(.width(32)) Reg25 (.D(WrData), .en(WrReg25), .Q(RegData25), .clk(Clock));  // open: clr
  Register #(.width(32)) Reg29 (.D(WrData), .en(WrReg29), .Q(RegData29), .clk(Clock));  // open: clr
  Register #(.width(32)) Reg2 (.D(WrData), .en(WrReg2), .Q(RegData2), .clk(Clock));  // open: clr
  Register #(.width(32)) Reg6 (.D(WrData), .en(WrReg6), .Q(RegData6), .clk(Clock));  // open: clr
  Register #(.width(32)) Reg10 (.D(WrData), .en(WrReg10), .Q(RegData10), .clk(Clock));  // open: clr
  Register #(.width(32)) Reg14 (.D(WrData), .en(WrReg14), .Q(RegData14), .clk(Clock));  // open: clr
  Register #(.width(32)) Reg18 (.D(WrData), .en(WrReg18), .Q(RegData18), .clk(Clock));  // open: clr
  Register #(.width(32)) Reg22 (.D(WrData), .en(WrReg22), .Q(RegData22), .clk(Clock));  // open: clr
  Register #(.width(32)) Reg26 (.D(WrData), .en(WrReg26), .Q(RegData26), .clk(Clock));  // open: clr
  Register #(.width(32)) Reg30 (.D(WrData), .en(WrReg30), .Q(RegData30), .clk(Clock));  // open: clr
  Register #(.width(32)) Reg3 (.D(WrData), .en(WrReg3), .Q(RegData3), .clk(Clock));  // open: clr
  Register #(.width(32)) Reg7 (.D(WrData), .en(WrReg7), .Q(RegData7), .clk(Clock));  // open: clr
  Register #(.width(32)) Reg11 (.D(WrData), .en(WrReg11), .Q(RegData11), .clk(Clock));  // open: clr
  Register #(.width(32)) Reg15 (.D(WrData), .en(WrReg15), .Q(RegData15), .clk(Clock));  // open: clr
  Register #(.width(32)) Reg19 (.D(WrData), .en(WrReg19), .Q(RegData19), .clk(Clock));  // open: clr
  Register #(.width(32)) Reg23 (.D(WrData), .en(WrReg23), .Q(RegData23), .clk(Clock));  // open: clr
  Register #(.width(32)) Reg27 (.D(WrData), .en(WrReg27), .Q(RegData27), .clk(Clock));  // open: clr
  Register #(.width(32)) Reg31 (.D(WrData), .en(WrReg31), .Q(RegData31), .clk(Clock));  // open: clr
  Multiplexer #(.select(5), .width(32), .enable("false")) multiplexer_1 (
    .in0({32{1'b0}}), .in1(RegData1), .in2(RegData2), .in3(RegData3), .in4(RegData4), .in5(RegData5),
    .in6(RegData6), .in7(RegData7), .in8(RegData8), .in9(RegData9), .in10(RegData10), .in11(RegData11),
    .in12(RegData12), .in13(RegData13), .in14(RegData14), .in15(RegData15), .in16(RegData16),
    .in17(RegData17), .in18(RegData18), .in19(RegData19), .in20(RegData20), .in21(RegData21),
    .in22(RegData22), .in23(RegData23), .in24(RegData24), .in25(RegData25), .in26(RegData26),
    .in27(RegData27), .in28(RegData28), .in29(RegData29), .in30(RegData30), .in31(RegData31), .out(RdData1),
    .sel(RdAddr1));
  Multiplexer #(.select(5), .width(32), .enable("false")) multiplexer_2 (
    .in0({32{1'b0}}), .in1(RegData1), .in2(RegData2), .in3(RegData3), .in4(RegData4), .in5(RegData5),
    .in6(RegData6), .in7(RegData7), .in8(RegData8), .in9(RegData9), .in10(RegData10), .in11(RegData11),
    .in12(RegData12), .in13(RegData13), .in14(RegData14), .in15(RegData15), .in16(RegData16),
    .in17(RegData17), .in18(RegData18), .in19(RegData19), .in20(RegData20), .in21(RegData21),
    .in22(RegData22), .in23(RegData23), .in24(RegData24), .in25(RegData25), .in26(RegData26),
    .in27(RegData27), .in28(RegData28), .in29(RegData29), .in30(RegData30), .in31(RegData31), .out(RdData2),
    .sel(RdAddr2));
endmodule

module Overflow (
  input  Add,
  input  Sub,
  input  ASign,
  input  BSign,
  input  ResultSign,
  output Overflow
);

  wire and_1_out, and_2_out, or_1_out, xnor_1_out, xor_1_out, xor_2_out;

  xnor xnor_1 (xnor_1_out, ASign, BSign);
  xor xor_1 (xor_1_out, ASign, BSign);
  and and_1 (and_1_out, xnor_1_out, Add);
  and and_2 (and_2_out, xor_1_out, Sub);
  or or_1 (or_1_out, and_1_out, and_2_out);
  xor xor_2 (xor_2_out, ResultSign, ASign);
  and and_3 (Overflow, or_1_out, xor_2_out);

  // Notes on the sheet:
  //   Overflow occurs when doing addition and sign(A) == sign(B) && sign(result) != sign(A)
  //   Or
  //   Overflow occurs when doing subtraction and sign(A) != sign(B) && sign(result) != sign(A)
endmodule

module PC (
  input  [31:0] PC_Input,
  input  Clock,
  output [31:0] PC_Output
);

  wire not_1_out;

  Register #(.width(32)) register_1 (.D(PC_Input), .Q(PC_Output), .clk(not_1_out));  // open: en, clr
  not not_1 (not_1_out, Clock);

  // Other names for the same wires on the sheet: PCin[31:0] = PC_Input; PCout[31:0] = PC_Output
endmodule

module InstrMem (
  input  [7:0] InstAddr,
  output [31:0] Instruction
);

  ROM #(.dataWidth(32)) rom_1 (.addr(InstAddr), .data(Instruction));  // open: sel

  // Notes on the sheet:
  //   contents of rom_1 (hex, n*v repeats v):
  //   20010005 34220003 3043ffff 612020 832822 243026 aca40064 8ca70064 22402a 10a80003 c44026 c000009
  //   1204820 3e00008
endmodule

module DataMem (
  input  [7:0] Address,
  input  [31:0] MemWrite,
  input  Write,
  input  Clock,
  input  Read,
  output [31:0] MemRead
);

  RAM #(.dataWidth(32), .bus("separate")) ram_1 (
    .addr(Address), .din(MemWrite), .data(MemRead), .str(Write), .clk(Clock), .ld(Read));  // open: sel, clr
endmodule

// Main Control
module Control (
  input  [5:0] Opcode,
  output ALUCtr0,
  output ALUCtrl1,
  output ALUCtrl2,
  output RegDst,
  output WrReg,
  output ALUSrc,
  output MemWrite,
  output MemtoReg,
  output MemRead,
  output Branch,
  output jump,
  output jal
);

  wire and_1_out, and_2_out, and_3_out, and_4_out, and_7_out, and_8_out, and_9_out, and_10_out, and_11_out,
       and_12_out, and_13_out, and_20_out, not_1_out, not_2_out, not_3_out, not_4_out, not_5_out, not_6_out,
       or_1_out;

  not not_1 (not_1_out, Opcode[5]);
  not not_2 (not_2_out, Opcode[2]);
  not not_3 (not_3_out, Opcode[3]);
  not not_4 (not_4_out, Opcode[4]);
  not not_5 (not_5_out, Opcode[1]);
  not not_6 (not_6_out, Opcode[0]);
  and and_1 (and_1_out, not_6_out, not_5_out, Opcode[2], not_3_out, not_4_out, not_1_out);
  and and_2 (and_2_out, Opcode[0], Opcode[1], not_2_out, not_4_out, Opcode[5]);
  and and_3 (and_3_out, not_6_out, not_5_out, not_2_out, Opcode[3], not_4_out, not_1_out);
  and and_4 (and_4_out, Opcode[0], Opcode[1], not_2_out, not_4_out, Opcode[5]);
  or or_1 (or_1_out, not_2_out, Opcode[2]);
  and and_5 (ALUCtrl2, Opcode[0], Opcode[1], Opcode[2], Opcode[3], Opcode[4], Opcode[5]);
  and and_6 (RegDst, not_6_out, not_5_out, not_2_out, not_3_out, not_4_out, not_1_out);
  and and_7 (and_7_out, not_6_out, not_5_out, not_2_out, not_3_out, not_4_out, not_1_out);
  and and_8 (and_8_out, Opcode[0], Opcode[1], not_2_out, not_3_out, not_4_out, Opcode[5]);
  and and_9 (and_9_out, not_5_out, Opcode[3], not_4_out, not_1_out);
  and and_10 (and_10_out, Opcode[0], Opcode[1], not_2_out, not_3_out, not_4_out, not_1_out);
  and and_11 (and_11_out, not_5_out, Opcode[3], not_4_out, not_1_out);
  and and_12 (and_12_out, not_6_out, not_5_out, Opcode[2], not_4_out, not_1_out);
  and and_13 (and_13_out, Opcode[0], Opcode[1], not_2_out, not_4_out, Opcode[5]);
  and and_14 (MemWrite, Opcode[0], Opcode[1], not_2_out, Opcode[3], not_4_out, Opcode[5]);
  and and_15 (MemtoReg, Opcode[0], Opcode[1], not_2_out, not_3_out, not_4_out, Opcode[5]);
  and and_16 (MemRead, Opcode[0], Opcode[1], not_2_out, not_3_out, not_4_out, Opcode[5]);
  and and_17 (Branch, not_6_out, not_5_out, Opcode[2], not_3_out, not_4_out, not_1_out);
  and and_18 (jump, not_6_out, Opcode[1], not_2_out, not_3_out, not_4_out, not_1_out);
  and and_19 (jal, Opcode[0], Opcode[1], not_2_out, not_3_out, not_4_out, not_1_out);
  and and_20 (and_20_out, not_6_out, not_5_out, or_1_out, Opcode[3], not_4_out, not_1_out);
  or or_2 (ALUSrc, and_11_out, and_12_out, and_13_out);
  or or_3 (ALUCtr0, and_1_out, and_2_out, and_3_out);
  or or_4 (ALUCtrl1, and_4_out, and_20_out);
  or or_5 (WrReg, and_7_out, and_8_out, and_9_out, and_10_out);
endmodule

module ALU_Control (
  input  [5:0] OpCode,
  input  [2:0] ALUOp,
  input  [5:0] funct,
  output [2:0] ALUCtrl,
  output jr
);

  wire and_1_out, and_2_out, and_3_out, and_4_out, not_1_out, not_2_out, not_3_out, not_4_out, not_5_out,
       not_6_out;
  wire [2:0] NewCtrl;

  not not_1 (not_1_out, funct[5]);
  not not_2 (not_2_out, funct[4]);
  not not_3 (not_3_out, funct[3]);
  not not_4 (not_4_out, funct[2]);
  not not_5 (not_5_out, funct[1]);
  not not_6 (not_6_out, funct[0]);
  and and_1 (and_1_out, ~OpCode[0], ~OpCode[1], ~OpCode[2], ~OpCode[3], ~OpCode[4], ~OpCode[5]);  // AND_Gate
  Multiplexer #(.width(3)) multiplexer_1 (.in0(ALUOp), .in1(NewCtrl), .out(ALUCtrl), .sel(and_1_out));  // open: en
  and and_2 (and_2_out, not_6_out, funct[1], funct[2], not_3_out, not_2_out, funct[5]);
  and and_3 (and_3_out, not_6_out, not_5_out, not_4_out, not_3_out, not_2_out, funct[5]);
  and and_4 (and_4_out, not_6_out, funct[1], not_4_out, funct[3], not_2_out, funct[5]);
  and and_5 (NewCtrl[1], not_6_out, not_5_out, not_3_out, not_2_out, funct[5]);
  and and_6 (NewCtrl[2], not_6_out, funct[1], not_4_out, not_2_out, funct[5]);
  and and_7 (jr, not_6_out, not_5_out, not_4_out, funct[3], not_2_out, not_1_out);
  or or_1 (NewCtrl[0], and_2_out, and_3_out, and_4_out);
endmodule

module Sign_Extend (
  input  [15:0] SEIn,
  output [31:0] SEOut
);


  assign SEOut = {{17{SEIn[15]}}, SEIn[14:0]};
endmodule

module SL2 (
  input  [31:0] in_1,
  output [31:0] out_2
);


  assign out_2 = {in_1[29:0], 2'b00};
endmodule
