// Logisim project Lab4.circ as structural Verilog: 15 circuits, main circuit main
module main (
);

  wire ALUSrc_D, ALUSrc_E, Branch_D, Clock, clock_1_out, comparator_1_eq, Jal_D, Jal_E, Jal_M, Jr_D, Jump_D,
       MemRead_D, MemRead_E, MemRead_M, MemtoReg_D, MemtoReg_E, MemtoReg_M, MemtoReg_W, MemWrite_D,
       MemWrite_E, MemWrite_M, not_2_out, or_1_out, or_2_out, RegDst_D, RegDst_E, RegWrite_D, RegWrite_E,
       RegWrite_M, RegWrite_W, Stall, TakeBranch, Zero_E, Zero_M;
  wire [1:0] BrFw_A, BrFw_B, Fw_A, Fw_B;
  wire [2:0] ALUCtrl_D, ALUCtrl_E;
  wire [4:0] multiplexer_8_out, Rd_E, RegDestAddr_E, RegDestAddr_M, Rs_E, Rt_E, WriteBackAddr;
  wire [5:0] Funct;
  wire [9:0] multiplexer_9_out;
  wire [15:6] iAddress;
  wire [31:0] adder_1_out, ALUResult_E, ALUResult_M, ALUResult_W, Instr_F, JrAddr, JumpAddr, MemData_M,
       MemData_W, multiplexer_1_out, multiplexer_2_out, multiplexer_3_out, multiplexer_4_out,
       multiplexer_5_out, multiplexer_7_out, multiplexer_10_out, multiplexer_13_out, multiplexer_14_out, PC,
       PC_4_D, PC_4_E, PC_4_F, PC_4_M, RDataA_D, RDataA_E, RDataB_D, RDataB_E, RDataB_M, SignExt_D,
       SignExt_E, WMemData_E, WMemData_M, WriteBackData;
  wire [31:16] Instr_D;

  Clock clock_1 (.out(clock_1_out));
  not not_1 (Clock, clock_1_out);
  // Probe on PC
  // Probe on Branch_D
  // Probe on Jump_D
  // Probe on Jal_D
  // Probe on Jr_D
  // Probe on RegWrite_W
  // Probe on WriteBackAddr
  // Probe on WriteBackData
  // Probe on ALUResult_M[7:0]
  // Probe on RDataB_M
  Adder #(.width(32)) adder_1 (.a(PC_4_D), .b(JumpAddr), .out(adder_1_out));  // open: cin, cout
  Multiplexer #(.width(32)) multiplexer_1 (
    .in0(PC_4_F), .in1(adder_1_out), .out(multiplexer_1_out), .sel(TakeBranch));  // open: en
  or or_1 (or_1_out, Jal_D, Jump_D);
  Multiplexer #(.width(32)) multiplexer_2 (
    .in0(multiplexer_1_out), .in1(JrAddr), .out(multiplexer_2_out), .sel(Jr_D));  // open: en
  Register #(.width(32)) PC_2 (.D(multiplexer_3_out), .en(not_2_out), .Q(PC), .clk(Clock));  // open: clr
  Multiplexer #(.width(32)) multiplexer_3 (
    .in0(multiplexer_2_out), .in1(JumpAddr), .out(multiplexer_3_out), .sel(or_1_out));  // open: en
  not not_2 (not_2_out, Stall);
  Adder #(.width(32)) adder_2 (.a(PC), .b(32'h4), .out(PC_4_F));  // open: cin, cout
  ROM #(.dataWidth(32)) rom_1 (.addr(PC[9:2]), .data(Instr_F));  // open: sel
  or or_2 (or_2_out, TakeBranch, Jump_D, Jr_D, Jal_D);
  Multiplexer #(.width(32)) multiplexer_4 (
    .in0(Instr_F), .in1({32{1'b0}}), .out(multiplexer_4_out), .sel(or_2_out));  // open: en
  Multiplexer #(.width(32)) multiplexer_5 (
    .in0(ALUResult_M), .in1(MemData_M), .out(multiplexer_5_out), .sel(MemtoReg_M));  // open: en
  IF_ID_Register if_id_register_1 (
    .PC_4_in(PC_4_F), .Instr_in(multiplexer_4_out), .PC_4_out(PC_4_D),
    .Instr_out({Instr_D, iAddress, Funct}), .Clock(Clock), .Stall(Stall));
  // Probe on {Instr_D, iAddress, Funct}
  Multiplexer #(.select(2), .width(32)) multiplexer_6 (
    .in0(RDataA_D), .in1(ALUResult_E), .in2(multiplexer_5_out), .in3(WriteBackData), .out(JrAddr),
    .sel(BrFw_A));  // open: en
  Multiplexer #(.select(2), .width(32)) multiplexer_7 (
    .in0(RDataB_D), .in1(ALUResult_E), .in2(multiplexer_5_out), .in3(WriteBackData), .out(multiplexer_7_out),
    .sel(BrFw_B));  // open: en
  RegFile regfile_1 (
    .WrAddr(WriteBackAddr), .WrData(WriteBackData), .WrReg(RegWrite_W), .RdAddr1(Instr_D[25:21]),
    .RdAddr2(Instr_D[20:16]), .RdData1(RDataA_D), .RdData2(RDataB_D), .Clock(Clock));
  Sign_Extend sign_extend_1 (.SEIn({iAddress, Funct}), .SEOut(SignExt_D));
  Comparator #(.width(32)) comparator_1 (.a(JrAddr), .b(multiplexer_7_out), .eq(comparator_1_eq));  // open: gt, lt
  Shift_Left_2 Shift_Left_2 (.in_1(SignExt_D), .out_2(JumpAddr));
  and and_1 (TakeBranch, comparator_1_eq, Branch_D);
  MainControl maincontrol_1 (
    .opcode(Instr_D[31:26]), .funct(Funct), .ALUCtrl(ALUCtrl_D), .RegDst(RegDst_D), .ALUSrc(ALUSrc_D),
    .MemRead(MemRead_D), .MemWrite(MemWrite_D), .RegWrite(RegWrite_D), .MemtoReg(MemtoReg_D),
    .Branch(Branch_D), .Jump(Jump_D), .Jal(Jal_D), .Jr(Jr_D));
  HazardControl hazardcontrol_1 (
    .MemRead_E(MemRead_E), .Rt_E(Rt_E), .Rs_D(Instr_D[25:21]), .Rt_D(Instr_D[20:16]), .Stall(Stall),
    .MemWrite_D(MemWrite_D));
  Multiplexer #(.width(5)) multiplexer_8 (
    .in0(Instr_D[20:16]), .in1({5{1'b1}}), .out(multiplexer_8_out), .sel(Jal_D));  // open: en
  Multiplexer #(.width(10)) multiplexer_9 (
    .in0({Jal_D, MemtoReg_D, RegWrite_D, MemWrite_D, MemRead_D, ALUSrc_D, RegDst_D, ALUCtrl_D}),
    .in1({10{1'b0}}), .out(multiplexer_9_out), .sel(Stall));  // open: en
  ID_EX_Register id_ex_register_1 (
    .Clock(Clock), .RDataA_In(RDataA_D), .RDataB_In(RDataB_D), .SignExt_In(SignExt_D),
    .Rt_In(multiplexer_8_out), .Rd_In(iAddress[15:11]), .RDataA_Out(RDataA_E), .RDataB_Out(RDataB_E),
    .SignExt_Out(SignExt_E), .Rt_Out(Rt_E), .Rd_Out(Rd_E), .PC_4_In(PC_4_D), .PC_4_out(PC_4_E),
    .ALUCtrl_In(multiplexer_9_out[2:0]), .ALUCtrl_Out(ALUCtrl_E), .RegDst_In(multiplexer_9_out[3]),
    .RegDst_Out(RegDst_E), .ALUSrc_In(multiplexer_9_out[4]), .ALUSrc_Out(ALUSrc_E),
    .MemRead_In(multiplexer_9_out[5]), .MemRead_Out(MemRead_E), .MemWrite_In(multiplexer_9_out[6]),
    .MemWrite_Out(MemWrite_E), .RegWrite_In(multiplexer_9_out[7]), .RegWrite_Out(RegWrite_E),
    .MemtoReg_In(multiplexer_9_out[8]), .MemtoReg_Out(MemtoReg_E), .Jal_In(multiplexer_9_out[9]),
    .Jal_Out(Jal_E), .Rs_In(Instr_D[25:21]), .Rs_Out(Rs_E));
  Multiplexer #(.select(2), .width(32)) multiplexer_10 (
    .in0(RDataA_E), .in1(ALUResult_M), .in2(WriteBackData), .in3(ALUResult_M), .out(multiplexer_10_out),
    .sel(Fw_A));  // open: en
  Multiplexer #(.select(2), .width(32)) multiplexer_11 (
    .in0(RDataB_E), .in1(ALUResult_M), .in2(WriteBackData), .in3(ALUResult_M), .out(WMemData_E), .sel(Fw_B));  // open: en
  Multiplexer #(.width(5)) multiplexer_12 (.in0(Rt_E), .in1(Rd_E), .out(RegDestAddr_E), .sel(RegDst_E));  // open: en
  Multiplexer #(.width(32)) multiplexer_13 (
    .in0(WMemData_E), .in1(SignExt_E), .out(multiplexer_13_out), .sel(ALUSrc_E));  // open: en
  ALU alu_1 (
    .ALUCtl(ALUCtrl_E), .A(multiplexer_10_out), .B(multiplexer_13_out), .ALUResult(ALUResult_E),
    .Zero(Zero_E), .Shamt(SignExt_E[10:6]));  // open: Overflow
  ForwardControl forwardcontrol_1 (
    .RegWrite_M(RegWrite_M), .Rs_E(Rs_E), .Rt_E(Rt_E), .RegDst_M(RegDestAddr_M), .FwA(Fw_A), .FwB(Fw_B),
    .RegDst_W(WriteBackAddr), .RegWrite_W(RegWrite_W), .Branch(Branch_D), .Rs_D(Instr_D[25:21]),
    .Rt_D(Instr_D[20:16]), .RegWrite_E(RegWrite_E), .RegDst_E(RegDestAddr_E), .BrFwA(BrFw_A), .BrFwB(BrFw_B));
  EX_MEM_Register ex_mem_register_1 (
    .Clock(Clock), .AddResult_In(PC_4_E), .AddResult_out(PC_4_M), .Zero_In(Zero_E), .Zero_Out(Zero_M),
    .ALUResult_In(ALUResult_E), .ALUResult_Out(ALUResult_M), .RegData_In(WMemData_E),
    .RegData_Out(WMemData_M), .RegDest_In(RegDestAddr_E), .RegDest_Out(RegDestAddr_M),
    .MemRead_In(MemRead_E), .MemRead_Out(MemRead_M), .MemWrite_In(MemWrite_E), .MemWrite_Out(MemWrite_M),
    .RegWrite_In(RegWrite_E), .RegWrite_Out(RegWrite_M), .MemtoReg_In(MemtoReg_E), .MemtoReg_Out(MemtoReg_M),
    .Jal_In(Jal_E), .Jal_Out(Jal_M));
  RAM #(.dataWidth(32), .bus("separate")) ram_1 (
    .addr(ALUResult_M[7:0]), .din(WMemData_M), .data(MemData_M), .str(MemWrite_M), .clk(Clock), .ld(MemRead_M));  // open: sel, clr
  Multiplexer #(.width(32)) multiplexer_14 (
    .in0(ALUResult_M), .in1(PC_4_M), .out(multiplexer_14_out), .sel(Jal_M));  // open: en
  MEM_WB_Register mem_wb_register_1 (
    .Clock(Clock), .MemData_In(MemData_M), .MemData_Out(MemData_W), .ALUResult_In(multiplexer_14_out),
    .ALUResult_Out(ALUResult_W), .RegDest_In(RegDestAddr_M), .RegDest_Out(WriteBackAddr),
    .RegWrite_In(RegWrite_M), .RegWrite_Out(RegWrite_W), .MemtoReg_In(MemtoReg_M), .MemtoReg_Out(MemtoReg_W));
  Multiplexer #(.width(32)) multiplexer_15 (
    .in0(ALUResult_W), .in1(MemData_W), .out(WriteBackData), .sel(MemtoReg_W));  // open: en

  // Other names for the same wires on the sheet: MemAddr_M[7:0] = ALUResult_M[7:0]; iAddress[5:0] = Funct;
  //   Instr_D[15:0] = {iAddress, Funct}; jAddress[25:0] = {Instr_D[25:16], iAddress, Funct};
  //   Shamt[4:0] = iAddress[10:6]; Rd_D[4:0] = iAddress[15:11]; Rt_D[4:0] = Instr_D[20:16];
  //   Rs_D[4:0] = Instr_D[25:21]; Opcode[5:0] = Instr_D[31:26]

  // Notes on the sheet:
  //   contents of rom_1 (hex, n*v repeats v):
  //   20010001 20020002 34030003 34040004 20050005 20060006 20070007 ac01000a 224020 8c6f0007 224824
  //   825022 a35825 e66027 a6682a c5702a 30300001 18a80 79082
  //   Flush Decode
  //   R-Type
  //   I-Type
  //   J-Type
endmodule

module _32bit (
  input  Add_Sub_control,
  input  [31:0] in_2,
  input  [31:0] in_3,
  output [31:0] out_4,
  output carry_out
);

  wire adder_1_cout, subtractor_1_bout;
  wire [31:0] adder_1_out, subtractor_1_out;

  Adder #(.width(32)) adder_1 (.a(in_2), .b(in_3), .out(adder_1_out), .cout(adder_1_cout));  // open: cin
  Subtractor #(.width(32)) subtractor_1 (
    .a(in_2), .b(in_3), .out(subtractor_1_out), .bout(subtractor_1_bout));  // open: bin
  Multiplexer #(.width(32), .enable("false")) multiplexer_1 (
    .in0(adder_1_out), .in1(subtractor_1_out), .out(out_4), .sel(Add_Sub_control));
  Multiplexer #(.enable("false")) multiplexer_2 (
    .in0(adder_1_cout), .in1(subtractor_1_bout), .out(carry_out), .sel(Add_Sub_control));
endmodule

module ALU (
  input  [2:0] ALUCtl,
  input  [31:0] A,
  input  [31:0] B,
  input  [4:0] Shamt,
  output [31:0] ALUResult,
  output Zero,
  output Overflow
);

  wire and_2_out, and_3_out, comparator_1_lt, not_1_out, not_2_out, not_3_out, or_2_out;
  wire [31:0] Add, And, LessThan, Nor, Or, ShiftLeft, ShiftRight, Sub;

  Adder #(.width(32)) adder_1 (.a(A), .b(B), .out(Add));  // open: cin, cout
  Subtractor #(.width(32)) subtractor_1 (.a(A), .b(B), .out(Sub));  // open: bin, bout
  assign And = A & B;  // AND_Gate and_1, 32 bits wide
  assign Or = A | B;  // OR_Gate or_1, 32 bits wide
  assign Nor = ~(A | B);  // NOR_Gate nor_1, 32 bits wide
  Comparator #(.width(32)) comparator_1 (.a(A), .b(B), .lt(comparator_1_lt));  // open: gt, eq
  assign LessThan = {{31{1'b0}}, comparator_1_lt};  // Bit_Extender bit_extender_1
  Shifter #(.width(32)) shifter_1 (.in(B), .\dist (Shamt), .out(ShiftLeft));
  Shifter #(.width(32), .shift("lr")) shifter_2 (.in(B), .\dist (Shamt), .out(ShiftRight));
  Multiplexer #(.select(3), .width(32), .enable("false")) multiplexer_1 (
    .in0(Add), .in1(Sub), .in2(And), .in3(Or), .in4(Nor), .in5(LessThan), .in6(ShiftLeft), .in7(ShiftRight),
    .out(ALUResult), .sel(ALUCtl));
  not not_1 (not_1_out, ALUCtl[0]);
  not not_2 (not_2_out, ALUCtl[1]);
  not not_3 (not_3_out, ALUCtl[2]);
  and and_2 (and_2_out, not_1_out, not_2_out, not_3_out);
  and and_3 (and_3_out, not_1_out, not_2_out, ALUCtl[2]);
  Overflow overflow_1 (
    .Add(and_2_out), .Sub(and_3_out), .ASign(A[31]), .BSign(B[31]), .ResultSign(ALUResult[31]),
    .Overflow(Overflow));
  not not_4 (Zero, or_2_out);
  or or_2 (or_2_out, ALUResult[0], ALUResult[1], ALUResult[2], ALUResult[3], ALUResult[4], ALUResult[5], ALUResult[6], ALUResult[7], ALUResult[8], ALUResult[9], ALUResult[10], ALUResult[11], ALUResult[12], ALUResult[13], ALUResult[14], ALUResult[15], ALUResult[16], ALUResult[17], ALUResult[18], ALUResult[19], ALUResult[20], ALUResult[21], ALUResult[22], ALUResult[23], ALUResult[24], ALUResult[25], ALUResult[26], ALUResult[27], ALUResult[28], ALUResult[29], ALUResult[30], ALUResult[31]);

  // Other names for the same wires on the sheet: ASign = A[31]; ResultSign = ALUResult[31]; BSign = B[31]

  // Notes on the sheet:
  //   To change AluCtl encodings, simpliy rearrange the tunnels
  //   You will also need to change the top two inputs to the overflow block to reflect the new encodings of Add and Sub
endmodule

module RegFile (
  input  [4:0] WrAddr,
  input  [31:0] WrData,
  input  WrReg,
  input  [4:0] RdAddr1,
  input  [4:0] RdAddr2,
  input  Clock,
  output [31:0] RdData1,
  output [31:0] RdData2
);

  wire and_1_out, and_2_out, comparator_1_eq, comparator_2_eq, comparator_3_eq, comparator_4_eq, not_1_out,
       not_2_out, WrReg0, WrReg1, WrReg2, WrReg3, WrReg4, WrReg5, WrReg6, WrReg7, WrReg8, WrReg9, WrReg10,
       WrReg11, WrReg12, WrReg13, WrReg14, WrReg15, WrReg16, WrReg17, WrReg18, WrReg19, WrReg20, WrReg21,
       WrReg22, WrReg23, WrReg24, WrReg25, WrReg26, WrReg27, WrReg28, WrReg29, WrReg30, WrReg31;
  wire [31:0] multiplexer_1_out, multiplexer_2_out, RegData1, RegData2, RegData3, RegData4, RegData5,
       RegData6, RegData7, RegData8, RegData9, RegData10, RegData11, RegData12, RegData13, RegData14,
       RegData15, RegData16, RegData17, RegData18, RegData19, RegData20, RegData21, RegData22, RegData23,
       RegData24, RegData25, RegData26, RegData27, RegData28, RegData29, RegData30, RegData31;

  Demultiplexer #(.select(5), .enable("false")) demultiplexer_1 (
    .out0(WrReg0), .out1(WrReg1), .out2(WrReg2), .out3(WrReg3), .out4(WrReg4), .out5(WrReg5), .out6(WrReg6),
    .out7(WrReg7), .out8(WrReg8), .out9(WrReg9), .out10(WrReg10), .out11(WrReg11), .out12(WrReg12),
    .out13(WrReg13), .out14(WrReg14), .out15(WrReg15), .out16(WrReg16), .out17(WrReg17), .out18(WrReg18),
    .out19(WrReg19), .out20(WrReg20), .out21(WrReg21), .out22(WrReg22), .out23(WrReg23), .out24(WrReg24),
    .out25(WrReg25), .out26(WrReg26), .out27(WrReg27), .out28(WrReg28), .out29(WrReg29), .out30(WrReg30),
    .out31(WrReg31), .in(WrReg), .sel(WrAddr));
  Register #(.width(32)) Reg4 (.D(WrData), .en(WrReg4), .Q(RegData4), .clk(Clock));  // open: clr
  Register #(.width(32)) Reg8 (.D(WrData), .en(WrReg8), .Q(RegData8), .clk(Clock));  // open: clr
  Register #(.width(32)) Reg12 (.D(WrData), .en(WrReg12), .Q(RegData12), .clk(Clock));  // open: clr
  Register #(.width(32)) Reg16 (.D(WrData), .en(WrReg16), .Q(RegData16), .clk(Clock));  // open: clr
  Register #(.width(32)) Reg20 (.D(WrData), .en(WrReg20), .Q(RegData20), .clk(Clock));  // open: clr
  Register #(.width(32)) Reg24 (.D(WrData), .en(WrReg24), .Q(RegData24), .clk(Clock));  // open: clr
  Register #(.width(32)) Reg28 (.D(WrData), .en(WrReg28), .Q(RegData28), .clk(Clock));  // open: clr
  Register #(.width(32)) Reg1 (.D(WrData), .en(WrReg1), .Q(RegData1), .clk(Clock));  // open: clr
  Register #(.width(32)) Reg5 (.D(WrData), .en(WrReg5), .Q(RegData5), .clk(Clock));  // open: clr
  Register #(.width(32)) Reg9 (.D(WrData), .en(WrReg9), .Q(RegData9), .clk(Clock));  // open: clr
  Register #(.width(32)) Reg13 (.D(WrData), .en(WrReg13), .Q(RegData13), .clk(Clock));  // open: clr
  Register #(.width(32)) Reg17 (.D(WrData), .en(WrReg17), .Q(RegData17), .clk(Clock));  // open: clr
  Register #(.width(32)) Reg21 (.D(WrData), .en(WrReg21), .Q(RegData21), .clk(Clock));  // open: clr
  Register #(.width(32)) Reg25 (.D(WrData), .en(WrReg25), .Q(RegData25), .clk(Clock));  // open: clr
  Register #(.width(32)) Reg29 (.D(WrData), .en(WrReg29), .Q(RegData29), .clk(Clock));  // open: clr
  Register #(.width(32)) Reg2 (.D(WrData), .en(WrReg2), .Q(RegData2), .clk(Clock));  // open: clr
  Register #(.width(32)) Reg6 (.D(WrData), .en(WrReg6), .Q(RegData6), .clk(Clock));  // open: clr
  Register #(.width(32)) Reg10 (.D(WrData), .en(WrReg10), .Q(RegData10), .clk(Clock));  // open: clr
  Register #(.width(32)) Reg14 (.D(WrData), .en(WrReg14), .Q(RegData14), .clk(Clock));  // open: clr
  Register #(.width(32)) Reg18 (.D(WrData), .en(WrReg18), .Q(RegData18), .clk(Clock));  // open: clr
  Register #(.width(32)) Reg22 (.D(WrData), .en(WrReg22), .Q(RegData22), .clk(Clock));  // open: clr
  Register #(.width(32)) Reg26 (.D(WrData), .en(WrReg26), .Q(RegData26), .clk(Clock));  // open: clr
  Register #(.width(32)) Reg30 (.D(WrData), .en(WrReg30), .Q(RegData30), .clk(Clock));  // open: clr
  Register #(.width(32)) Reg3 (.D(WrData), .en(WrReg3), .Q(RegData3), .clk(Clock));  // open: clr
  Register #(.width(32)) Reg7 (.D(WrData), .en(WrReg7), .Q(RegData7), .clk(Clock));  // open: clr
  Register #(.width(32)) Reg11 (.D(WrData), .en(WrReg11), .Q(RegData11), .clk(Clock));  // open: clr
  Register #(.width(32)) Reg15 (.D(WrData), .en(WrReg15), .Q(RegData15), .clk(Clock));  // open: clr
  Register #(.width(32)) Reg19 (.D(WrData), .en(WrReg19), .Q(RegData19), .clk(Clock));  // open: clr
  Register #(.width(32)) Reg23 (.D(WrData), .en(WrReg23), .Q(RegData23), .clk(Clock));  // open: clr
  Register #(.width(32)) Reg27 (.D(WrData), .en(WrReg27), .Q(RegData27), .clk(Clock));  // open: clr
  Register #(.width(32)) Reg31 (.D(WrData), .en(WrReg31), .Q(RegData31), .clk(Clock));  // open: clr
  Multiplexer #(.select(5), .width(32), .enable("false")) multiplexer_1 (
    .in0({32{1'b0}}), .in1(RegData1), .in2(RegData2), .in3(RegData3), .in4(RegData4), .in5(RegData5),
    .in6(RegData6), .in7(RegData7), .in8(RegData8), .in9(RegData9), .in10(RegData10), .in11(RegData11),
    .in12(RegData12), .in13(RegData13), .in14(RegData14), .in15(RegData15), .in16(RegData16),
    .in17(RegData17), .in18(RegData18), .in19(RegData19), .in20(RegData20), .in21(RegData21),
    .in22(RegData22), .in23(RegData23), .in24(RegData24), .in25(RegData25), .in26(RegData26),
    .in27(RegData27), .in28(RegData28), .in29(RegData29), .in30(RegData30), .in31(RegData31),
    .out(multiplexer_1_out), .sel(RdAddr1));
  Multiplexer #(.select(5), .width(32), .enable("false")) multiplexer_2 (
    .in0({32{1'b0}}), .in1(RegData1), .in2(RegData2), .in3(RegData3), .in4(RegData4), .in5(RegData5),
    .in6(RegData6), .in7(RegData7), .in8(RegData8), .in9(RegData9), .in10(RegData10), .in11(RegData11),
    .in12(RegData12), .in13(RegData13), .in14(RegData14), .in15(RegData15), .in16(RegData16),
    .in17(RegData17), .in18(RegData18), .in19(RegData19), .in20(RegData20), .in21(RegData21),
    .in22(RegData22), .in23(RegData23), .in24(RegData24), .in25(RegData25), .in26(RegData26),
    .in27(RegData27), .in28(RegData28), .in29(RegData29), .in30(RegData30), .in31(RegData31),
    .out(multiplexer_2_out), .sel(RdAddr2));
  Multiplexer #(.width(32), .enable("false")) multiplexer_3 (
    .in0(multiplexer_1_out), .in1(WrData), .out(RdData1), .sel(and_1_out));
  Multiplexer #(.width(32), .enable("false")) multiplexer_4 (
    .in0(multiplexer_2_out), .in1(WrData), .out(RdData2), .sel(and_2_out));
  Comparator #(.width(5), .mode("unsigned")) comparator_1 (
    .a(WrAddr), .b(RdAddr1), .eq(comparator_1_eq));  // open: gt, lt
  and and_1 (and_1_out, comparator_1_eq, WrReg, not_1_out);
  Comparator #(.width(5), .mode("unsigned")) comparator_2 (
    .a(WrAddr), .b(RdAddr2), .eq(comparator_2_eq));  // open: gt, lt
  and and_2 (and_2_out, comparator_2_eq, WrReg, not_2_out);
  Comparator #(.width(5), .mode("unsigned")) comparator_3 (
    .a(WrAddr), .b({5{1'b0}}), .eq(comparator_3_eq));  // open: gt, lt
  not not_1 (not_1_out, comparator_3_eq);
  Comparator #(.width(5), .mode("unsigned")) comparator_4 (
    .a(WrAddr), .b({5{1'b0}}), .eq(comparator_4_eq));  // open: gt, lt
  not not_2 (not_2_out, comparator_4_eq);
endmodule

module Overflow (
  input  Add,
  input  Sub,
  input  ASign,
  input  BSign,
  input  ResultSign,
  output Overflow
);

  wire and_1_out, and_2_out, or_1_out, xnor_1_out, xor_1_out, xor_2_out;

  xnor xnor_1 (xnor_1_out, ASign, BSign);
  xor xor_1 (xor_1_out, ASign, BSign);
  and and_1 (and_1_out, xnor_1_out, Add);
  and and_2 (and_2_out, xor_1_out, Sub);
  or or_1 (or_1_out, and_1_out, and_2_out);
  xor xor_2 (xor_2_out, ResultSign, ASign);
  and and_3 (Overflow, or_1_out, xor_2_out);

  // Notes on the sheet:
  //   Overflow occurs when doing addition and sign(A) == sign(B) && sign(result) != sign(A)
  //   Or
  //   Overflow occurs when doing subtraction and sign(A) != sign(B) && sign(result) != sign(A)
endmodule

module IF_ID_Register (
  input  Clock,
  input  Stall,
  input  [31:0] PC_4_in,
  input  [31:0] Instr_in,
  output [31:0] PC_4_out,
  output [31:0] Instr_out
);

  wire not_1_out, not_2_out;

  not not_1 (not_1_out, Stall);
  not not_2 (not_2_out, Stall);
  Register #(.width(32)) register_1 (.D(PC_4_in), .en(not_1_out), .Q(PC_4_out), .clk(Clock));  // open: clr
  Register #(.width(32)) register_2 (.D(Instr_in), .en(not_2_out), .Q(Instr_out), .clk(Clock));  // open: clr
endmodule

module ID_EX_Register (
  input  Clock,
  input  [2:0] ALUCtrl_In,
  input  [31:0] PC_4_In,
  input  RegDst_In,
  input  [31:0] RDataA_In,
  input  ALUSrc_In,
  input  [31:0] RDataB_In,
  input  MemRead_In,
  input  Jal_In,
  input  [31:0] SignExt_In,
  input  MemWrite_In,
  input  [4:0] Rt_In,
  input  RegWrite_In,
  input  [4:0] Rd_In,
  input  MemtoReg_In,
  input  [4:0] Rs_In,
  output [2:0] ALUCtrl_Out,
  output [31:0] PC_4_out,
  output RegDst_Out,
  output [31:0] RDataA_Out,
  output ALUSrc_Out,
  output [31:0] RDataB_Out,
  output MemRead_Out,
  output Jal_Out,
  output [31:0] SignExt_Out,
  output MemWrite_Out,
  output [4:0] Rt_Out,
  output RegWrite_Out,
  output [4:0] Rd_Out,
  output MemtoReg_Out,
  output [4:0] Rs_Out
);

  Register #(.width(32)) register_1 (.D(PC_4_In), .Q(PC_4_out), .clk(Clock));  // open: en, clr
  Register #(.width(32)) register_2 (.D(RDataA_In), .Q(RDataA_Out), .clk(Clock));  // open: en, clr
  Register #(.width(32)) register_3 (.D(RDataB_In), .Q(RDataB_Out), .clk(Clock));  // open: en, clr
  Register #(.width(32)) register_4 (.D(SignExt_In), .Q(SignExt_Out), .clk(Clock));  // open: en, clr
  Register #(.width(5)) register_5 (.D(Rt_In), .Q(Rt_Out), .clk(Clock));  // open: en, clr
  Register #(.width(5)) register_6 (.D(Rd_In), .Q(Rd_Out), .clk(Clock));  // open: en, clr
  Register #(.width(5)) register_7 (.D(Rs_In), .Q(Rs_Out), .clk(Clock));  // open: en, clr
  Register #(.width(3)) register_8 (.D(ALUCtrl_In), .Q(ALUCtrl_Out), .clk(Clock));  // open: en, clr
  Register #(.width(1)) register_9 (.D(RegDst_In), .Q(RegDst_Out), .clk(Clock));  // open: en, clr
  Register #(.width(1)) register_10 (.D(ALUSrc_In), .Q(ALUSrc_Out), .clk(Clock));  // open: en, clr
  Register #(.width(1)) register_11 (.D(MemRead_In), .Q(MemRead_Out), .clk(Clock));  // open: en, clr
  Register #(.width(1)) register_12 (.D(MemWrite_In), .Q(MemWrite_Out), .clk(Clock));  // open: en, clr
  Register #(.width(1)) register_13 (.D(RegWrite_In), .Q(RegWrite_Out), .clk(Clock));  // open: en, clr
  Register #(.width(1)) register_14 (.D(MemtoReg_In), .Q(MemtoReg_Out), .clk(Clock));  // open: en, clr
  Register #(.width(1)) register_15 (.D(Jal_In), .Q(Jal_Out), .clk(Clock));  // open: en, clr

  // Notes on the sheet:
  //   Control Signals
endmodule

module EX_MEM_Register (
  input  Clock,
  input  MemRead_In,
  input  [31:0] AddResult_In,
  input  MemWrite_In,
  input  Zero_In,
  input  RegWrite_In,
  input  MemtoReg_In,
  input  Jal_In,
  input  [31:0] ALUResult_In,
  input  [31:0] RegData_In,
  input  [4:0] RegDest_In,
  output MemRead_Out,
  output [31:0] AddResult_out,
  output MemWrite_Out,
  output Zero_Out,
  output RegWrite_Out,
  output MemtoReg_Out,
  output Jal_Out,
  output [31:0] ALUResult_Out,
  output [31:0] RegData_Out,
  output [4:0] RegDest_Out
);

  Register #(.width(32)) register_1 (.D(AddResult_In), .Q(AddResult_out), .clk(Clock));  // open: en, clr
  Register #(.width(1)) register_2 (.D(Zero_In), .Q(Zero_Out), .clk(Clock));  // open: en, clr
  Register #(.width(32)) register_3 (.D(ALUResult_In), .Q(ALUResult_Out), .clk(Clock));  // open: en, clr
  Register #(.width(32)) register_4 (.D(RegData_In), .Q(RegData_Out), .clk(Clock));  // open: en, clr
  Register #(.width(5)) register_5 (.D(RegDest_In), .Q(RegDest_Out), .clk(Clock));  // open: en, clr
  Register #(.width(1)) register_6 (.D(MemRead_In), .Q(MemRead_Out), .clk(Clock));  // open: en, clr
  Register #(.width(1)) register_7 (.D(MemWrite_In), .Q(MemWrite_Out), .clk(Clock));  // open: en, clr
  Register #(.width(1)) register_8 (.D(RegWrite_In), .Q(RegWrite_Out), .clk(Clock));  // open: en, clr
  Register #(.width(1)) register_9 (.D(MemtoReg_In), .Q(MemtoReg_Out), .clk(Clock));  // open: en, clr
  Register #(.width(1)) register_10 (.D(Jal_In), .Q(Jal_Out), .clk(Clock));  // open: en, clr

  // Notes on the sheet:
  //   Control Signals
endmodule

module MEM_WB_Register (
  input  Clock,
  input  [31:0] MemData_In,
  input  RegWrite_In,
  input  [31:0] ALUResult_In,
  input  MemtoReg_In,
  input  [4:0] RegDest_In,
  output [31:0] MemData_Out,
  output RegWrite_Out,
  output [31:0] ALUResult_Out,
  output MemtoReg_Out,
  output [4:0] RegDest_Out
);

  Register #(.width(32)) register_1 (.D(MemData_In), .Q(MemData_Out), .clk(Clock));  // open: en, clr
  Register #(.width(32)) register_2 (.D(ALUResult_In), .Q(ALUResult_Out), .clk(Clock));  // open: en, clr
  Register #(.width(5)) register_3 (.D(RegDest_In), .Q(RegDest_Out), .clk(Clock));  // open: en, clr
  Register #(.width(1)) register_4 (.D(RegWrite_In), .Q(RegWrite_Out), .clk(Clock));  // open: en, clr
  Register #(.width(1)) register_5 (.D(MemtoReg_In), .Q(MemtoReg_Out), .clk(Clock));  // open: en, clr

  // Notes on the sheet:
  //   Control Signals
endmodule

module Sign_Extend (
  input  [15:0] SEIn,
  output [31:0] SEOut
);


  assign SEOut = {{17{SEIn[15]}}, SEIn[14:0]};
endmodule

module Sign_ExtendJ (
  input  [25:0] SEIn,
  output [31:0] SEOut
);


  assign SEOut = {{7{SEIn[25]}}, SEIn[24:0]};
endmodule

module Shift_Left_2 (
  input  [31:0] in_1,
  output [31:0] out_2
);


  assign out_2 = {in_1[29:0], 2'b00};
endmodule

module MainControl (
  input  [5:0] opcode,
  input  [5:0] funct,
  output [2:0] ALUCtrl,
  output RegDst,
  output ALUSrc,
  output MemRead,
  output MemWrite,
  output RegWrite,
  output MemtoReg,
  output Branch,
  output Jump,
  output Jal,
  output Jr
);

  wire and_1_out, and_2_out, and_4_out, and_5_out, and_6_out, and_9_out, and_10_out, and_11_out, and_18_out,
       and_19_out, and_20_out, and_21_out, and_22_out, and_23_out, and_24_out, and_25_out, and_27_out, Jr_t,
       not_1_out, not_2_out, not_3_out, not_4_out, not_5_out, not_6_out, or_1_out;
  wire [1:0] ALUOp;
  wire [2:0] NewCtrl;
  wire [5:0] not_7_out;

  not not_1 (not_1_out, opcode[5]);
  not not_2 (not_2_out, opcode[4]);
  and and_1 (and_1_out, opcode[3], opcode[0]);
  and and_2 (and_2_out, ~opcode[3], ~opcode[0]);  // AND_Gate
  not not_3 (not_3_out, opcode[1]);
  not not_4 (not_4_out, opcode[5]);
  not not_5 (not_5_out, opcode[4]);
  not not_6 (not_6_out, opcode[1]);
  and and_3 (RegDst, ~opcode[5], ~opcode[4], ~opcode[3], ~opcode[2], ~opcode[1], ~opcode[0]);  // AND_Gate
  and and_4 (and_4_out, ~opcode[5], opcode[3], ~opcode[2], ~opcode[1], ~opcode[0]);  // AND_Gate
  and and_5 (and_5_out, opcode[5], ~opcode[2], opcode[1], opcode[0]);  // AND_Gate
  and and_6 (and_6_out, ~opcode[5], opcode[3], opcode[2], ~opcode[1]);  // AND_Gate
  and and_7 (MemRead, opcode[5], ~opcode[3], ~opcode[2], opcode[1], opcode[0]);  // AND_Gate
  and and_8 (MemWrite, opcode[5], opcode[3], ~opcode[2], opcode[1], opcode[0]);  // AND_Gate
  and and_9 (and_9_out, ~opcode[5], ~opcode[2], ~opcode[1], ~opcode[0]);  // AND_Gate
  and and_10 (and_10_out, ~opcode[3], ~opcode[2], opcode[1], opcode[0]);  // AND_Gate
  and and_11 (and_11_out, ~opcode[5], opcode[3], opcode[2], ~opcode[1]);  // AND_Gate
  and and_12 (MemtoReg, opcode[5], ~opcode[3], ~opcode[2], opcode[1], opcode[0]);  // AND_Gate
  and and_13 (Branch, ~opcode[5], ~opcode[3], opcode[2], ~opcode[1], ~opcode[0]);  // AND_Gate
  and and_14 (Jump, ~opcode[5], ~opcode[3], ~opcode[2], opcode[1], ~opcode[0]);  // AND_Gate
  and and_15 (Jal, ~opcode[5], ~opcode[3], ~opcode[2], opcode[1], opcode[0]);  // AND_Gate
  or or_1 (or_1_out, and_1_out, and_2_out);
  and and_16 (ALUOp[1], not_4_out, not_5_out, opcode[3], opcode[2], not_6_out);
  or or_2 (ALUSrc, and_4_out, and_5_out, and_6_out);
  or or_3 (RegWrite, and_9_out, and_10_out, and_11_out);
  and and_17 (ALUOp[0], not_1_out, not_2_out, or_1_out, opcode[2], not_3_out);
  assign not_7_out = ~opcode;  // NOT_Gate not_7, 6 bits wide
  and and_18 (and_18_out, funct[5], ~funct[2], funct[1], ~funct[0]);  // AND_Gate
  and and_19 (and_19_out, funct[5], ~funct[3], funct[2], ~funct[1], funct[0]);  // AND_Gate
  and and_20 (and_20_out, ~funct[5], ~funct[3], ~funct[2], funct[1], ~funct[0]);  // AND_Gate
  and and_21 (and_21_out, funct[5], ~funct[3], funct[2], ~funct[1]);  // AND_Gate
  and and_22 (and_22_out, ~funct[5], ~funct[3], ~funct[2], ~funct[0]);  // AND_Gate
  and and_23 (and_23_out, funct[5], ~funct[3], funct[2], funct[1], funct[0]);  // AND_Gate
  and and_24 (and_24_out, funct[5], funct[3], ~funct[2], funct[1], ~funct[0]);  // AND_Gate
  and and_25 (and_25_out, ~funct[5], ~funct[3], ~funct[2], ~funct[0]);  // AND_Gate
  and and_26 (Jr_t, ~funct[5], funct[3], ~funct[2], ~funct[1], ~funct[0]);  // AND_Gate
  or or_4 (NewCtrl[0], and_18_out, and_19_out, and_20_out);
  or or_5 (NewCtrl[1], and_21_out, and_22_out);
  or or_6 (NewCtrl[2], and_23_out, and_24_out, and_25_out);
  and and_27 (and_27_out, not_7_out[0], not_7_out[1], not_7_out[2], not_7_out[3], not_7_out[4], not_7_out[5]);
  Multiplexer #(.width(3)) multiplexer_1 (
    .in0({1'b0, ALUOp}), .in1(NewCtrl), .out(ALUCtrl), .sel(and_27_out));  // open: en
  and and_28 (Jr, and_27_out, Jr_t);

  // Notes on the sheet:
  //   Not Needed outside R-Type
endmodule

module ForwardControl (
  input  RegWrite_E,
  input  RegWrite_M,
  input  Branch,
  input  RegWrite_W,
  input  [4:0] Rs_D,
  input  [4:0] Rs_E,
  input  [4:0] Rt_D,
  input  [4:0] Rt_E,
  input  [4:0] RegDst_E,
  input  [4:0] RegDst_M,
  input  [4:0] RegDst_W,
  output [1:0] FwA,
  output [1:0] BrFwA,
  output [1:0] FwB,
  output [1:0] BrFwB
);

  wire and_5_out, and_6_out, and_7_out, and_8_out, and_9_out, and_10_out, not_1_out, not_2_out, not_3_out,
       not_4_out, not_5_out, not_6_out, not_7_out, not_8_out, not_9_out, not_10_out, or_1_out, or_2_out,
       or_3_out, or_4_out, or_5_out, or_6_out, or_7_out, or_8_out, or_9_out, or_10_out, or_11_out, or_12_out,
       or_13_out, or_14_out, or_15_out, or_16_out, or_17_out, or_18_out, or_19_out, or_20_out;
  wire [1:0] multiplexer_1_out, multiplexer_2_out, multiplexer_3_out, multiplexer_4_out;
  wire [4:0] xor_1_out, xor_2_out, xor_3_out, xor_4_out, xor_5_out, xor_6_out, xor_7_out, xor_8_out,
       xor_9_out, xor_10_out, xor_11_out, xor_12_out, xor_13_out, xor_14_out, xor_15_out, xor_16_out,
       xor_17_out, xor_18_out, xor_19_out, xor_20_out;

  assign xor_1_out = RegDst_M ^ Rs_E;  // XOR_Gate xor_1, 5 bits wide
  assign xor_2_out = RegDst_M ^ {5{1'b0}};  // XOR_Gate xor_2, 5 bits wide
  assign xor_3_out = RegDst_W ^ Rs_E;  // XOR_Gate xor_3, 5 bits wide
  assign xor_4_out = RegDst_W ^ {5{1'b0}};  // XOR_Gate xor_4, 5 bits wide
  assign xor_5_out = RegDst_M ^ Rt_E;  // XOR_Gate xor_5, 5 bits wide
  assign xor_6_out = RegDst_M ^ {5{1'b0}};  // XOR_Gate xor_6, 5 bits wide
  assign xor_7_out = RegDst_W ^ Rt_E;  // XOR_Gate xor_7, 5 bits wide
  assign xor_8_out = RegDst_W ^ {5{1'b0}};  // XOR_Gate xor_8, 5 bits wide
  or or_1 (or_1_out, xor_1_out[0], xor_1_out[1], xor_1_out[2], xor_1_out[3], xor_1_out[4]);
  not not_1 (not_1_out, or_1_out);
  or or_2 (or_2_out, xor_2_out[0], xor_2_out[1], xor_2_out[2], xor_2_out[3], xor_2_out[4]);
  or or_3 (or_3_out, xor_3_out[0], xor_3_out[1], xor_3_out[2], xor_3_out[3], xor_3_out[4]);
  not not_2 (not_2_out, or_3_out);
  or or_4 (or_4_out, xor_4_out[0], xor_4_out[1], xor_4_out[2], xor_4_out[3], xor_4_out[4]);
  not not_3 (not_3_out, or_5_out);
  or or_5 (or_5_out, xor_5_out[0], xor_5_out[1], xor_5_out[2], xor_5_out[3], xor_5_out[4]);
  or or_6 (or_6_out, xor_6_out[0], xor_6_out[1], xor_6_out[2], xor_6_out[3], xor_6_out[4]);
  or or_7 (or_7_out, xor_7_out[0], xor_7_out[1], xor_7_out[2], xor_7_out[3], xor_7_out[4]);
  not not_4 (not_4_out, or_7_out);
  or or_8 (or_8_out, xor_8_out[0], xor_8_out[1], xor_8_out[2], xor_8_out[3], xor_8_out[4]);
  and and_1 (FwA[0], RegWrite_M, not_1_out, or_2_out);
  and and_2 (FwA[1], RegWrite_W, not_2_out, or_4_out);
  and and_3 (FwB[0], RegWrite_M, not_3_out, or_6_out);
  and and_4 (FwB[1], RegWrite_W, not_4_out, or_8_out);
  assign xor_9_out = RegDst_E ^ Rs_D;  // XOR_Gate xor_9, 5 bits wide
  assign xor_10_out = RegDst_E ^ {5{1'b0}};  // XOR_Gate xor_10, 5 bits wide
  assign xor_11_out = RegDst_M ^ Rs_D;  // XOR_Gate xor_11, 5 bits wide
  assign xor_12_out = RegDst_M ^ {5{1'b0}};  // XOR_Gate xor_12, 5 bits wide
  assign xor_13_out = RegDst_W ^ Rs_D;  // XOR_Gate xor_13, 5 bits wide
  assign xor_14_out = RegDst_W ^ {5{1'b0}};  // XOR_Gate xor_14, 5 bits wide
  assign xor_15_out = RegDst_E ^ Rt_D;  // XOR_Gate xor_15, 5 bits wide
  assign xor_16_out = RegDst_E ^ {5{1'b0}};  // XOR_Gate xor_16, 5 bits wide
  assign xor_17_out = RegDst_M ^ Rt_D;  // XOR_Gate xor_17, 5 bits wide
  assign xor_18_out = RegDst_M ^ {5{1'b0}};  // XOR_Gate xor_18, 5 bits wide
  assign xor_19_out = RegDst_W ^ Rt_D;  // XOR_Gate xor_19, 5 bits wide
  assign xor_20_out = RegDst_W ^ {5{1'b0}};  // XOR_Gate xor_20, 5 bits wide
  or or_9 (or_9_out, xor_9_out[0], xor_9_out[1], xor_9_out[2], xor_9_out[3], xor_9_out[4]);
  or or_10 (or_10_out, xor_10_out[0], xor_10_out[1], xor_10_out[2], xor_10_out[3], xor_10_out[4]);
  or or_11 (or_11_out, xor_11_out[0], xor_11_out[1], xor_11_out[2], xor_11_out[3], xor_11_out[4]);
  or or_12 (or_12_out, xor_12_out[0], xor_12_out[1], xor_12_out[2], xor_12_out[3], xor_12_out[4]);
  or or_13 (or_13_out, xor_13_out[0], xor_13_out[1], xor_13_out[2], xor_13_out[3], xor_13_out[4]);
  or or_14 (or_14_out, xor_14_out[0], xor_14_out[1], xor_14_out[2], xor_14_out[3], xor_14_out[4]);
  or or_15 (or_15_out, xor_15_out[0], xor_15_out[1], xor_15_out[2], xor_15_out[3], xor_15_out[4]);
  or or_16 (or_16_out, xor_16_out[0], xor_16_out[1], xor_16_out[2], xor_16_out[3], xor_16_out[4]);
  or or_17 (or_17_out, xor_17_out[0], xor_17_out[1], xor_17_out[2], xor_17_out[3], xor_17_out[4]);
  or or_18 (or_18_out, xor_18_out[0], xor_18_out[1], xor_18_out[2], xor_18_out[3], xor_18_out[4]);
  or or_19 (or_19_out, xor_19_out[0], xor_19_out[1], xor_19_out[2], xor_19_out[3], xor_19_out[4]);
  or or_20 (or_20_out, xor_20_out[0], xor_20_out[1], xor_20_out[2], xor_20_out[3], xor_20_out[4]);
  and and_5 (and_5_out, RegWrite_E, not_5_out, or_10_out);
  not not_5 (not_5_out, or_9_out);
  not not_6 (not_6_out, or_11_out);
  and and_6 (and_6_out, RegWrite_M, not_6_out, or_12_out);
  and and_7 (and_7_out, RegWrite_W, not_7_out, or_14_out);
  not not_7 (not_7_out, or_13_out);
  and and_8 (and_8_out, RegWrite_E, not_8_out, or_16_out);
  not not_8 (not_8_out, or_15_out);
  not not_9 (not_9_out, or_17_out);
  and and_9 (and_9_out, RegWrite_M, not_9_out, or_18_out);
  and and_10 (and_10_out, RegWrite_W, not_10_out, or_20_out);
  not not_10 (not_10_out, or_19_out);
  Multiplexer #(.width(2)) multiplexer_1 (
    .in0(2'b00), .in1(2'b11), .out(multiplexer_1_out), .sel(and_7_out));  // open: en
  Multiplexer #(.width(2)) multiplexer_2 (
    .in0(2'b00), .in1(2'b11), .out(multiplexer_2_out), .sel(and_10_out));  // open: en
  Multiplexer #(.width(2)) multiplexer_3 (
    .in0(multiplexer_1_out), .in1(2'b10), .out(multiplexer_3_out), .sel(and_6_out));  // open: en
  Multiplexer #(.width(2)) multiplexer_4 (
    .in0(multiplexer_2_out), .in1(2'b10), .out(multiplexer_4_out), .sel(and_9_out));  // open: en
  Multiplexer #(.width(2)) multiplexer_5 (
    .in0(multiplexer_3_out), .in1(2'b01), .out(BrFwA), .sel(and_5_out));  // open: en
  Multiplexer #(.width(2)) multiplexer_6 (
    .in0(multiplexer_4_out), .in1(2'b01), .out(BrFwB), .sel(and_8_out));  // open: en

  // Notes on the sheet:
  //   Branch Forwarding
endmodule

module HazardControl (
  input  MemWrite_D,
  input  MemRead_E,
  input  [4:0] Rt_E,
  input  [4:0] Rs_D,
  input  [4:0] Rt_D,
  output Stall
);

  wire not_1_out, not_2_out, not_3_out, or_1_out, or_2_out, or_3_out, or_4_out;
  wire [4:0] xor_1_out, xor_2_out, xor_3_out;

  not not_1 (not_1_out, MemWrite_D);
  assign xor_1_out = Rt_E ^ Rs_D;  // XOR_Gate xor_1, 5 bits wide
  assign xor_2_out = Rt_E ^ Rt_D;  // XOR_Gate xor_2, 5 bits wide
  assign xor_3_out = Rt_E ^ {5{1'b0}};  // XOR_Gate xor_3, 5 bits wide
  or or_1 (or_1_out, xor_1_out[0], xor_1_out[1], xor_1_out[2], xor_1_out[3], xor_1_out[4]);
  or or_2 (or_2_out, xor_2_out[0], xor_2_out[1], xor_2_out[2], xor_2_out[3], xor_2_out[4]);
  or or_3 (or_3_out, xor_3_out[0], xor_3_out[1], xor_3_out[2], xor_3_out[3], xor_3_out[4]);
  not not_2 (not_2_out, or_1_out);
  not not_3 (not_3_out, or_2_out);
  or or_4 (or_4_out, not_2_out, not_3_out);
  and and_1 (Stall, not_1_out, MemRead_E, or_4_out, or_3_out);
endmodule
